// Logisim project alu.circ as structural Verilog: 17 circuits, main circuit main
module main (
  input  [15:0] input_0,
  input  [15:0] input_1,
  input  R_type,
  input  [3:0] switch,
  output [15:0] \output ,
  output sign_OF,
  output unsign_OF,
  output Equal
);

  ALU alu_1 (
    .in_1(input_0), .in_2(input_1), .S(switch), .out_7(\output ), .out_8(Equal), .out_5(unsign_OF),
    .out_6(sign_OF), .R_type(R_type));
endmodule

module OR (
  input  [15:0] in_1,
  input  [15:0] in_2,
  output [15:0] out_3
);

  assign out_3 = in_1 | in_2;  // OR_Gate or_1, 16 bits wide
endmodule

module AND (
  input  [15:0] in_1,
  input  [15:0] in_2,
  output [15:0] out_3
);

  assign out_3 = in_1 & in_2;  // AND_Gate and_1, 16 bits wide
endmodule

module add_1bit (
  input  A,
  input  B,
  input  Carry_In,
  output Carry_Out,
  output SUM
);

  wire and_1_out, and_2_out, and_3_out, and_4_out, and_5_out, and_6_out, and_7_out, and_8_out;

  and and_1 (and_1_out, B, Carry_In);
  and and_2 (and_2_out, A, Carry_In);
  and and_3 (and_3_out, B, A);
  and and_4 (and_4_out, A, B, Carry_In);
  and and_5 (and_5_out, A, ~B, ~Carry_In);  // AND_Gate
  and and_6 (and_6_out, ~A, B, ~Carry_In);  // AND_Gate
  and and_7 (and_7_out, ~A, ~B, Carry_In);  // AND_Gate
  and and_8 (and_8_out, A, B, Carry_In);
  or or_1 (Carry_Out, and_1_out, and_2_out, and_3_out, and_4_out);
  or or_2 (SUM, and_5_out, and_6_out, and_7_out, and_8_out);
endmodule

module add_8bit (
  input  [7:0] in_1,
  input  Cin,
  input  [7:0] in_3,
  output out_4,
  output [7:0] Sum,
  output Unsigned_OF
);

  wire add_1bit_1_carry_out, add_1bit_2_carry_out, add_1bit_3_carry_out, add_1bit_4_carry_out,
       add_1bit_5_carry_out, add_1bit_6_carry_out, add_1bit_7_carry_out, bitselector_1_out,
       bitselector_2_out, bitselector_3_out;

  add_1bit add_1bit_1 (.A(in_1[0]), .B(in_3[0]), .Carry_In(Cin), .Carry_Out(add_1bit_1_carry_out), .SUM(Sum[0]));
  add_1bit add_1bit_2 (
    .A(in_1[1]), .B(in_3[1]), .Carry_In(add_1bit_1_carry_out), .Carry_Out(add_1bit_2_carry_out), .SUM(Sum[1]));
  add_1bit add_1bit_3 (
    .A(in_1[2]), .B(in_3[2]), .Carry_In(add_1bit_2_carry_out), .Carry_Out(add_1bit_3_carry_out), .SUM(Sum[2]));
  add_1bit add_1bit_4 (
    .A(in_1[3]), .B(in_3[3]), .Carry_In(add_1bit_3_carry_out), .Carry_Out(add_1bit_4_carry_out), .SUM(Sum[3]));
  add_1bit add_1bit_5 (
    .A(in_1[4]), .B(in_3[4]), .Carry_In(add_1bit_4_carry_out), .Carry_Out(add_1bit_5_carry_out), .SUM(Sum[4]));
  add_1bit add_1bit_6 (
    .A(in_1[5]), .B(in_3[5]), .Carry_In(add_1bit_5_carry_out), .Carry_Out(add_1bit_6_carry_out), .SUM(Sum[5]));
  add_1bit add_1bit_7 (
    .A(in_1[6]), .B(in_3[6]), .Carry_In(add_1bit_6_carry_out), .Carry_Out(add_1bit_7_carry_out), .SUM(Sum[6]));
  add_1bit add_1bit_8 (
    .A(in_1[7]), .B(in_3[7]), .Carry_In(add_1bit_7_carry_out), .Carry_Out(Unsigned_OF), .SUM(Sum[7]));
  BitSelector bitselector_1 (.in(in_1), .out(bitselector_1_out), .sel(3'b111));
  BitSelector bitselector_2 (.in(in_3), .out(bitselector_2_out), .sel(3'b111));
  BitSelector bitselector_3 (.in(Sum), .out(bitselector_3_out), .sel(3'b111));
  signed_overflow signed_overflow_1 (
    .A_sig(bitselector_1_out), .B_sig(bitselector_2_out), .Sum_sig(bitselector_3_out), .Sum_OF(out_4));  // open: Sub_sig, Sub_OF

  // Notes on the sheet:
  //   A
  //   B
endmodule

module ADD (
  input  [15:0] in_1,
  input  [15:0] in_2,
  output out_3,
  output [15:0] out_4,
  output unsigned_OF
);

  wire add_8bit_1_unsigned_of, bitselector_1_out, bitselector_2_out, bitselector_3_out;

  add_8bit add_8bit_1 (
    .in_1(in_1[7:0]), .in_3(in_2[7:0]), .Unsigned_OF(add_8bit_1_unsigned_of), .Sum(out_4[7:0]), .Cin(1'b0));  // open: out_4
  add_8bit add_8bit_2 (
    .in_1(in_1[15:8]), .in_3(in_2[15:8]), .Unsigned_OF(unsigned_OF), .Sum(out_4[15:8]),
    .Cin(add_8bit_1_unsigned_of));  // open: out_4
  BitSelector #(.width(16)) bitselector_1 (.in(in_1), .out(bitselector_1_out), .sel(4'b1111));
  BitSelector #(.width(16)) bitselector_2 (.in(in_2), .out(bitselector_2_out), .sel(4'b1111));
  BitSelector #(.width(16)) bitselector_3 (.in(out_4), .out(bitselector_3_out), .sel(4'b1111));
  signed_overflow signed_overflow_1 (
    .A_sig(bitselector_1_out), .B_sig(bitselector_2_out), .Sum_sig(bitselector_3_out), .Sum_OF(out_3));  // open: Sub_sig, Sub_OF

  // Notes on the sheet:
  //   sigbit
endmodule

module sub_8bit (
  input  in_1,
  input  [7:0] A_8bit,
  input  [7:0] B_8bit,
  output out_4,
  output [7:0] SUM,
  output out_6
);

  wire add_1bit_1_carry_out, add_1bit_2_carry_out, add_1bit_3_carry_out, add_1bit_4_carry_out,
       add_1bit_5_carry_out, add_1bit_6_carry_out, add_1bit_7_carry_out, bitselector_1_out,
       bitselector_2_out, bitselector_3_out;
  wire [7:0] not_1_out;

  assign not_1_out = ~B_8bit;  // NOT_Gate not_1, 8 bits wide
  add_1bit add_1bit_1 (
    .A(A_8bit[0]), .B(not_1_out[0]), .Carry_In(in_1), .Carry_Out(add_1bit_1_carry_out), .SUM(SUM[0]));
  add_1bit add_1bit_2 (
    .A(A_8bit[1]), .B(not_1_out[1]), .Carry_In(add_1bit_1_carry_out), .Carry_Out(add_1bit_2_carry_out),
    .SUM(SUM[1]));
  add_1bit add_1bit_3 (
    .A(A_8bit[2]), .B(not_1_out[2]), .Carry_In(add_1bit_2_carry_out), .Carry_Out(add_1bit_3_carry_out),
    .SUM(SUM[2]));
  add_1bit add_1bit_4 (
    .A(A_8bit[3]), .B(not_1_out[3]), .Carry_In(add_1bit_3_carry_out), .Carry_Out(add_1bit_4_carry_out),
    .SUM(SUM[3]));
  add_1bit add_1bit_5 (
    .A(A_8bit[4]), .B(not_1_out[4]), .Carry_In(add_1bit_4_carry_out), .Carry_Out(add_1bit_5_carry_out),
    .SUM(SUM[4]));
  add_1bit add_1bit_6 (
    .A(A_8bit[5]), .B(not_1_out[5]), .Carry_In(add_1bit_5_carry_out), .Carry_Out(add_1bit_6_carry_out),
    .SUM(SUM[5]));
  add_1bit add_1bit_7 (
    .A(A_8bit[6]), .B(not_1_out[6]), .Carry_In(add_1bit_6_carry_out), .Carry_Out(add_1bit_7_carry_out),
    .SUM(SUM[6]));
  add_1bit add_1bit_8 (
    .A(A_8bit[7]), .B(not_1_out[7]), .Carry_In(add_1bit_7_carry_out), .Carry_Out(out_6), .SUM(SUM[7]));
  BitSelector bitselector_1 (.in(A_8bit), .out(bitselector_1_out), .sel(3'b111));
  BitSelector bitselector_2 (.in(B_8bit), .out(bitselector_2_out), .sel(3'b111));
  BitSelector bitselector_3 (.in(SUM), .out(bitselector_3_out), .sel(3'b111));
  signed_overflow signed_overflow_1 (
    .A_sig(bitselector_1_out), .B_sig(bitselector_2_out), .Sub_sig(bitselector_3_out), .Sub_OF(out_4));  // open: Sum_sig, Sum_OF

  // Other names for the same wires on the sheet: A[7:0] = A_8bit; B[7:0] = B_8bit

  // Notes on the sheet:
  //   Set to +1 s.t. for two's comp
endmodule

module SLL (
  input  [15:0] in_1,
  input  [15:0] in_2,
  input  rtype,
  output [15:0] out_4
);

  wire [3:0] multiplexer_2_out;
  wire [15:0] multiplexer_1_out;

  Multiplexer #(.width(16), .enable("false")) multiplexer_1 (
    .in0(in_2), .in1(in_1), .out(multiplexer_1_out), .sel(rtype));
  Multiplexer #(.width(4), .enable("false")) multiplexer_2 (
    .in0(4'b1000), .in1(in_2[3:0]), .out(multiplexer_2_out), .sel(rtype));
  Shifter #(.width(16)) shifter_1 (.in(multiplexer_1_out), .\dist (multiplexer_2_out), .out(out_4));

  // Other names for the same wires on the sheet: R = rtype

  // Notes on the sheet:
  //   for case for lui if not r-type shift input B by 8
endmodule

module SRL (
  input  [15:0] in_1,
  input  [15:0] in_2,
  output [15:0] out_3
);

  wire [3:0] bitselector_1_out;

  BitSelector #(.width(16), .group(4)) bitselector_1 (.in(in_2), .out(bitselector_1_out), .sel(2'b00));
  Shifter #(.width(16), .shift("lr")) shifter_1 (.in(in_1), .\dist (bitselector_1_out), .out(out_3));
endmodule

module SRA (
  input  [15:0] in_1,
  input  [15:0] in_2,
  output [15:0] out_3
);

  wire [3:0] bitselector_1_out;

  BitSelector #(.width(16), .group(4)) bitselector_1 (.in(in_2), .out(bitselector_1_out), .sel(2'b00));
  Shifter #(.width(16), .shift("ar")) shifter_1 (.in(in_1), .\dist (bitselector_1_out), .out(out_3));

  // Notes on the sheet:
  //   In
endmodule

module SLT (
  input  [15:0] in_1,
  input  [15:0] in_2,
  output [15:0] out_3
);

  wire comparator_1_lt;

  Comparator #(.width(16)) comparator_1 (.a(in_1), .b(in_2), .lt(comparator_1_lt));  // open: gt, eq
  assign out_3 = {{15{1'b0}}, comparator_1_lt};  // Bit_Extender bit_extender_1
endmodule

module signed_overflow (
  input  A_sig,
  input  B_sig,
  input  Sum_sig,
  input  Sub_sig,
  output Sum_OF,
  output Sub_OF
);

  wire and_1_out, and_2_out, and_3_out, and_4_out;

  and and_1 (and_1_out, ~A_sig, ~B_sig, Sum_sig);  // AND_Gate
  and and_2 (and_2_out, A_sig, B_sig, ~Sum_sig);  // AND_Gate
  and and_3 (and_3_out, A_sig, ~B_sig, ~Sub_sig);  // AND_Gate
  and and_4 (and_4_out, ~A_sig, B_sig, Sub_sig);  // AND_Gate
  or or_1 (Sum_OF, and_1_out, and_2_out);
  or or_2 (Sub_OF, and_3_out, and_4_out);
endmodule

module ADDP8 (
  input  [15:0] in_1,
  input  [15:0] in_2,
  output [15:0] out_3,
  output sign_OF,
  output unsign_OF
);

  wire A, add_8bit_1_out_4, add_8bit_2_out_4, B;

  add_8bit add_8bit_1 (
    .in_1(in_1[7:0]), .in_3(in_2[7:0]), .Unsigned_OF(A), .Sum(out_3[7:0]), .Cin(1'b0),
    .out_4(add_8bit_1_out_4));
  add_8bit add_8bit_2 (
    .in_1(in_1[15:8]), .in_3(in_2[15:8]), .Unsigned_OF(B), .Sum(out_3[15:8]), .Cin(1'b0),
    .out_4(add_8bit_2_out_4));
  or or_1 (sign_OF, add_8bit_1_out_4, add_8bit_2_out_4);
  or or_2 (unsign_OF, A, B);
endmodule

module SUBP8 (
  input  [15:0] in_1,
  input  [15:0] in_2,
  output [15:0] out_3,
  output sign_OF
);

  wire C, D;

  or or_1 (sign_OF, C, D);
  sub_8bit sub_8bit_1 (
    .A_8bit(in_1[7:0]), .B_8bit(in_2[7:0]), .SUM(out_3[7:0]), .out_4(C), .in_1(1'b1));  // open: out_6
  sub_8bit sub_8bit_2 (
    .A_8bit(in_1[15:8]), .B_8bit(in_2[15:8]), .SUM(out_3[15:8]), .out_4(D), .in_1(1'b1));  // open: out_6
endmodule

module SUB (
  input  [15:0] in_1,
  input  [15:0] in_2,
  output out_3,
  output [15:0] out_4
);

  wire bitselector_1_out, bitselector_2_out, bitselector_3_out, sub_8bit_1_out_6;

  sub_8bit sub_8bit_1 (
    .A_8bit(in_1[7:0]), .B_8bit(in_2[7:0]), .out_6(sub_8bit_1_out_6), .SUM(out_4[7:0]), .in_1(1'b1));  // open: out_4
  sub_8bit sub_8bit_2 (
    .A_8bit(in_1[15:8]), .B_8bit(in_2[15:8]), .SUM(out_4[15:8]), .in_1(sub_8bit_1_out_6));  // open: out_6, out_4
  BitSelector #(.width(16)) bitselector_1 (.in(in_1), .out(bitselector_1_out), .sel(4'b1111));
  BitSelector #(.width(16)) bitselector_2 (.in(in_2), .out(bitselector_2_out), .sel(4'b1111));
  BitSelector #(.width(16)) bitselector_3 (.in(out_4), .out(bitselector_3_out), .sel(4'b1111));
  signed_overflow signed_overflow_1 (
    .A_sig(bitselector_1_out), .B_sig(bitselector_2_out), .Sub_sig(bitselector_3_out), .Sub_OF(out_3));  // open: Sum_sig, Sum_OF
endmodule

module SLTP8 (
  input  [15:0] in_1,
  input  [15:0] in_2,
  output [15:0] out_3
);

  wire comparator_1_lt, comparator_2_lt;

  Comparator comparator_1 (.a(in_1[7:0]), .b(in_2[7:0]), .lt(comparator_1_lt));  // open: gt, eq
  Comparator comparator_2 (.a(in_1[15:8]), .b(in_2[15:8]), .lt(comparator_2_lt));  // open: gt, eq
  assign out_3[7:0] = {{7{1'b0}}, comparator_1_lt};  // Bit_Extender bit_extender_1
  assign out_3[15:8] = {{7{1'b0}}, comparator_2_lt};  // Bit_Extender bit_extender_2
endmodule

// A
module ALU (
  input  [15:0] in_1,
  input  [15:0] in_2,
  input  [3:0] S,
  input  R_type,
  output out_5,
  output out_6,
  output [15:0] out_7,
  output out_8
);

  wire s_OF_add, s_OF_ap8, s_OF_sp8, s_OF_sub, us_OF_add, us_OF_ap8;
  wire [15:0] add_1_out_4, addp8_1_out_3, and_1_out_3, or_1_out_3, sll_1_out_4, slt_1_out_3, sltp8_1_out_3,
       sra_1_out_3, srl_1_out_3, sub_1_out_4, subp8_1_out_3;

  // Probe on sll_1_out_4
  OR or_1 (.in_1(in_1), .in_2(in_2), .out_3(or_1_out_3));
  AND and_1 (.in_1(in_1), .in_2(in_2), .out_3(and_1_out_3));
  ADD add_1 (.in_1(in_1), .in_2(in_2), .unsigned_OF(us_OF_add), .out_3(s_OF_add), .out_4(add_1_out_4));
  SUB sub_1 (.in_1(in_1), .in_2(in_2), .out_3(s_OF_sub), .out_4(sub_1_out_4));
  SLL sll_1 (.in_1(in_1), .out_4(sll_1_out_4), .in_2(in_2), .rtype(R_type));
  SRL srl_1 (.in_1(in_1), .out_3(srl_1_out_3), .in_2(in_2));
  SRA sra_1 (.in_1(in_1), .out_3(sra_1_out_3), .in_2(in_2));
  SLT slt_1 (.in_1(in_1), .in_2(in_2), .out_3(slt_1_out_3));
  ADDP8 addp8_1 (.in_1(in_1), .in_2(in_2), .out_3(addp8_1_out_3), .sign_OF(us_OF_ap8), .unsign_OF(s_OF_ap8));
  SUBP8 subp8_1 (.in_1(in_1), .in_2(in_2), .out_3(subp8_1_out_3), .sign_OF(s_OF_sp8));
  SLTP8 sltp8_1 (.in_1(in_1), .in_2(in_2), .out_3(sltp8_1_out_3));
  Multiplexer #(.select(4), .width(16), .enable("false")) multiplexer_1 (
    .in0(or_1_out_3), .in1(and_1_out_3), .in2(add_1_out_4), .in3(sub_1_out_4), .in4(sll_1_out_4),
    .in5(srl_1_out_3), .in6(sra_1_out_3), .in7(slt_1_out_3), .in8(addp8_1_out_3), .in9(subp8_1_out_3),
    .in10(sltp8_1_out_3), .in11({16{1'b0}}), .in12({16{1'b0}}), .in13({16{1'b0}}), .in14({16{1'b0}}),
    .in15({16{1'b0}}), .out(out_7), .sel(S));
  Comparator #(.width(16)) comparator_1 (.a(in_2), .b(in_1), .eq(out_8));  // open: gt, lt
  Multiplexer #(.select(4), .enable("false")) multiplexer_2 (
    .in0(1'b0), .in1(1'b0), .in2(us_OF_add), .in3(1'b0), .in4(1'b0), .in5(1'b0), .in6(1'b0), .in7(1'b0),
    .in8(us_OF_ap8), .in9(1'b0), .in10(1'b0), .in11(1'b0), .in12(1'b0), .in13(1'b0), .in14(1'b0),
    .in15(1'b0), .out(out_5), .sel(S));
  Multiplexer #(.select(4), .enable("false")) multiplexer_3 (
    .in0(1'b0), .in1(1'b0), .in2(s_OF_add), .in3(s_OF_sub), .in4(1'b0), .in5(1'b0), .in6(1'b0), .in7(1'b0),
    .in8(s_OF_ap8), .in9(s_OF_sp8), .in10(1'b0), .in11(1'b0), .in12(1'b0), .in13(1'b0), .in14(1'b0),
    .in15(1'b0), .out(out_6), .sel(S));

  // Other names for the same wires on the sheet: A[15:0] = in_1; B[15:0] = in_2; R_flag = R_type; switch[3:0] = S

  // Notes on the sheet:
  //   Input A
  //   Input B
  //   RESULT_MUX
  //   UNSIGNED OVERFLOW?
  //   EQUAL?
  //   OUTPUT
  //   SIGNED OVERFLOW?
endmodule
