// Logisim project cpu.circ as structural Verilog: 11 circuits, main circuit cpu_connect
module main (
  input  [15:0] From_Instr_Mem,
  input  clk,
  output [15:0] r0,
  output [15:0] r1,
  output [15:0] r2,
  output [15:0] r3,
  output [15:0] Display_0,
  output [15:0] Display_1,
  output [15:0] To_Instr_Mem,
  output [15:0] Data_Mem_Data,
  output [15:0] Data_Mem_Addr,
  output Data_Mem_Write
);

  cpu_connect cpu_connect_1 (
    .From_Instr_Mem(From_Instr_Mem), .r0(r0), .r1(r1), .r2(r2), .r3(r3), .Display_0(Display_0),
    .Display_1(Display_1), .clk(clk), .To_Instr_Mem(To_Instr_Mem), .Data_Mem_Data(Data_Mem_Data),
    .Data_Mem_Addr(Data_Mem_Addr), .Data_Mem_Write(Data_Mem_Write));

  // Other names for the same wires on the sheet: d0[15:0] = Display_0; d1[15:0] = Display_1
endmodule

// 4
module cpu_connect (
  input  [15:0] From_Instr_Mem,
  input  clk,
  output [15:0] r0,
  output [15:0] r1,
  output [15:0] r2,
  output [15:0] r3,
  output [15:0] Display_0,
  output [15:0] Display_1,
  output [15:0] To_Instr_Mem,
  output [15:0] Data_Mem_Data,
  output [15:0] Data_Mem_Addr,
  output Data_Mem_Write
);

  wire ALUSrc, beq, bitselector_1_out, blockbottom_1_out_5, blockbottom_1_out_6, blockbottom_1_out_7,
       blockbottom_1_out_8, blockbottom_1_out_9, blockbottom_1_out_10, blockbottom_1_out_11,
       blockbottom_1_out_12, blockbottom_1_out_13, blockbottom_1_out_14, blockbottom_1_out_15,
       blockbottom_1_out_16, blockbottom_1_out_17, blockbottom_1_out_18, blockbottom_1_out_19,
       blockbottom_1_out_20, blockbottom_2_out_5, blockbottom_2_out_6, blockbottom_2_out_7,
       blockbottom_2_out_8, blockbottom_2_out_9, blockbottom_2_out_10, blockbottom_2_out_11,
       blockbottom_2_out_12, blockbottom_2_out_13, blockbottom_2_out_14, blockbottom_2_out_15,
       blockbottom_2_out_16, blockbottom_2_out_17, blockbottom_2_out_18, blockbottom_2_out_19,
       blockbottom_2_out_20, blocktop_1_out_5, blocktop_1_out_6, blocktop_1_out_7, blocktop_1_out_8,
       blocktop_1_out_9, blocktop_1_out_10, blocktop_1_out_11, blocktop_1_out_12, blocktop_1_out_13,
       blocktop_1_out_14, blocktop_1_out_15, blocktop_1_out_16, blocktop_1_out_17, blocktop_1_out_18,
       blocktop_1_out_19, blocktop_1_out_20, blocktop_2_out_5, blocktop_2_out_6, blocktop_2_out_7,
       blocktop_2_out_8, blocktop_2_out_9, blocktop_2_out_10, blocktop_2_out_11, blocktop_2_out_12,
       blocktop_2_out_13, blocktop_2_out_14, blocktop_2_out_15, blocktop_2_out_16, blocktop_2_out_17,
       blocktop_2_out_18, blocktop_2_out_19, blocktop_2_out_20, Branch, disp, equal, jal, jr, Jump, MemRead,
       MemtoReg, no_op, not_1_out, overflow, R_type, Reg_Dest, RegWrite;
  wire [1:0] multiplexer_2_out, multiplexer_4_out, RD, RS, RT;
  wire [3:0] alu_switch_1_alu_switch, ALUOp, opcode;
  wire [5:0] funct;
  wire [7:0] decode_1_immediate;
  wire [11:0] decode_1_addr;
  wire [15:0] ADDR, and_1_out, br_PC, Data_1, Data_2, dec_inc_pc_1_inc_pc_2, dec_inc_pc_2_dec_pc_2,
       dec_inc_pc_3_dec_pc_2, IMM, multiplexer_1_out, multiplexer_3_out, multiplexer_5_out,
       multiplexer_6_out, multiplexer_7_out, or_1_out, register_1_q, write_data;

  // Probe on multiplexer_1_out
  Multiplexer #(.width(16), .enable("false")) multiplexer_1 (
    .in0(From_Instr_Mem), .in1({16{1'b0}}), .out(multiplexer_1_out), .sel(no_op));
  decode decode_1 (
    .instruction(register_1_q), .RS(RS), .RT(RT), .RD(RD), .FUNCT(funct), .IMMEDIATE(decode_1_immediate),
    .ADDR(decode_1_addr), .OPCODE(opcode));
  Register #(.width(16)) register_1 (.D(multiplexer_1_out), .en(1'b1), .Q(register_1_q), .clk(clk));  // open: clr
  // Probe on multiplexer_3_out
  Sign_Ext sign_ext_1 (.addr(decode_1_addr), .imm(decode_1_immediate), .in_3(MemRead), .se_addr(ADDR), .se_imm(IMM));
  to_noop to_noop_1 (.beq(beq), .equal(equal), .branch(Branch), .jr(jr), .jal(jal), .jump(Jump), .nop(no_op));
  Register #(.width(16)) register_2 (.D(multiplexer_3_out), .en(1'b1), .Q(To_Instr_Mem), .clk(clk));  // open: clr
  // Probe on multiplexer_2_out
  Multiplexer #(.width(2), .enable("false")) multiplexer_2 (
    .in0(RT), .in1(RD), .out(multiplexer_2_out), .sel(Reg_Dest));
  Multiplexer #(.width(16), .enable("false")) multiplexer_3 (
    .in0(multiplexer_5_out), .in1(Data_1), .out(multiplexer_3_out), .sel(jr));
  dec_inc_pc dec_inc_pc_1 (.inc_pc(To_Instr_Mem), .inc_pc_2(dec_inc_pc_1_inc_pc_2));  // open: dec_pc, dec_pc_2
  dec_inc_pc dec_inc_pc_2 (.dec_pc(To_Instr_Mem), .dec_pc_2(dec_inc_pc_2_dec_pc_2));  // open: inc_pc, inc_pc_2
  Multiplexer #(.width(2), .enable("false")) multiplexer_4 (
    .in0(multiplexer_2_out), .in1(2'b11), .out(multiplexer_4_out), .sel(jal));
  CONTROL control_1 (
    .opcode(opcode), .Reg_Dest(Reg_Dest), .Branch(Branch), .Jump(Jump), .Extend(MemRead), .Mem_reg(MemtoReg),
    .Mem_write(Data_Mem_Write), .ALUSrc(ALUSrc), .Reg_Write(RegWrite), .Rtype(R_type), .Display(disp),
    .JAL(jal), .JR(jr), .BEQ(beq), .ALU_op(ALUOp));
  Branch branch_1 (
    .pc(dec_inc_pc_1_inc_pc_2), .imm(IMM), .branch(Branch), .equal(equal), .BEQ_BNE(beq), .pc_branch(br_PC));
  assign and_1_out = dec_inc_pc_2_dec_pc_2 & 16'hf000;  // AND_Gate and_1, 16 bits wide
  Multiplexer #(.width(16), .enable("false")) multiplexer_5 (
    .in0(br_PC), .in1(or_1_out), .out(multiplexer_5_out), .sel(Jump));
  assign or_1_out = and_1_out | ADDR;  // OR_Gate or_1, 16 bits wide
  Regfile_main main_1 (
    .Read_register_1(RS), .Read_register_2(RT), .write_register(multiplexer_4_out), .write_data(write_data),
    .Reg_0_Value(r0), .Reg_1_Value(r1), .Reg_2_Value(r2), .Reg_3_Value(r3), .RegWrite(RegWrite), .clock(clk),
    .Read_Data_1(Data_1), .Read_Data_2(Data_2));
  // Probe on Data_2
  // Probe on IMM
  // Probe on multiplexer_6_out
  // Probe on Data_1
  Multiplexer #(.width(16), .enable("false")) multiplexer_6 (
    .in0(Data_2), .in1(IMM), .out(multiplexer_6_out), .sel(ALUSrc));
  // Probe on funct[3:0]
  // Probe on ALUOp
  alu_main main_2 (
    .input_0(Data_1), .input_1(multiplexer_6_out), .R_type(R_type), .switch(alu_switch_1_alu_switch),
    .\output (Data_Mem_Addr), .sign_OF(overflow), .Equal(equal));  // open: unsign_OF
  alu_switch alu_switch_1 (.alu_switch(alu_switch_1_alu_switch), .R_flag(R_type), .I_type(ALUOp), .Rtype(funct[3:0]));
  _7_Segment_Display u_7_segment_display_1 (
    .g(blocktop_1_out_5), .f(blocktop_1_out_13), .a(blocktop_1_out_14), .b(blocktop_1_out_6),
    .e(blockbottom_1_out_13), .d(blockbottom_1_out_5), .c(blockbottom_1_out_6), .dp(blockbottom_1_out_14));
  BlockBottom blockbottom_1 (
    .out_13(blockbottom_1_out_13), .out_5(blockbottom_1_out_5), .out_6(blockbottom_1_out_6),
    .out_14(blockbottom_1_out_14), .out_15(blockbottom_1_out_15), .out_7(blockbottom_1_out_7),
    .out_8(blockbottom_1_out_8), .out_16(blockbottom_1_out_16), .out_17(blockbottom_1_out_17),
    .out_9(blockbottom_1_out_9), .out_10(blockbottom_1_out_10), .out_18(blockbottom_1_out_18),
    .out_19(blockbottom_1_out_19), .out_11(blockbottom_1_out_11), .out_12(blockbottom_1_out_12),
    .out_20(blockbottom_1_out_20), .in_1(Display_0[15:12]), .in_2(Display_0[11:8]), .in_3(Display_0[7:4]),
    .in_4(Display_0[3:0]));
  // Probe on Data_Mem_Addr
  // Probe on alu_switch_1_alu_switch
  BlockTop blocktop_1 (
    .in_1(Display_0[15:12]), .in_2(Display_0[11:8]), .in_3(Display_0[7:4]), .in_4(Display_0[3:0]),
    .out_5(blocktop_1_out_5), .out_13(blocktop_1_out_13), .out_14(blocktop_1_out_14),
    .out_6(blocktop_1_out_6), .out_7(blocktop_1_out_7), .out_15(blocktop_1_out_15),
    .out_16(blocktop_1_out_16), .out_8(blocktop_1_out_8), .out_9(blocktop_1_out_9),
    .out_17(blocktop_1_out_17), .out_18(blocktop_1_out_18), .out_10(blocktop_1_out_10),
    .out_11(blocktop_1_out_11), .out_19(blocktop_1_out_19), .out_20(blocktop_1_out_20),
    .out_12(blocktop_1_out_12));
  _7_Segment_Display u_7_segment_display_2 (
    .g(blocktop_1_out_9), .f(blocktop_1_out_17), .a(blocktop_1_out_18), .b(blocktop_1_out_10),
    .e(blockbottom_1_out_17), .d(blockbottom_1_out_9), .c(blockbottom_1_out_10), .dp(blockbottom_1_out_18));
  _7_Segment_Display u_7_segment_display_3 (
    .g(blocktop_1_out_7), .f(blocktop_1_out_15), .a(blocktop_1_out_16), .b(blocktop_1_out_8),
    .e(blockbottom_1_out_15), .d(blockbottom_1_out_7), .c(blockbottom_1_out_8), .dp(blockbottom_1_out_16));
  not not_1 (not_1_out, Data_Mem_Write);
  _7_Segment_Display u_7_segment_display_4 (
    .g(blocktop_1_out_11), .f(blocktop_1_out_19), .a(blocktop_1_out_20), .b(blocktop_1_out_12),
    .e(blockbottom_1_out_19), .d(blockbottom_1_out_11), .c(blockbottom_1_out_12), .dp(blockbottom_1_out_20));
  assign Data_Mem_Data = Data_Mem_Write ? Data_2 : 16'bz;  // Controlled_Buffer controlled_buffer_1
  RAM #(.addrWidth(16), .dataWidth(16)) ram_1 (
    .addr(Data_Mem_Addr), .data(Data_Mem_Data), .sel(1'b1), .clk(clk), .ld(not_1_out));  // open: clr
  _7_Segment_Display u_7_segment_display_5 (
    .g(blocktop_2_out_5), .f(blocktop_2_out_13), .a(blocktop_2_out_14), .b(blocktop_2_out_6),
    .e(blockbottom_2_out_13), .d(blockbottom_2_out_5), .c(blockbottom_2_out_6), .dp(blockbottom_2_out_14));
  _7_Segment_Display u_7_segment_display_6 (
    .g(blocktop_2_out_7), .f(blocktop_2_out_15), .a(blocktop_2_out_16), .b(blocktop_2_out_8),
    .e(blockbottom_2_out_15), .d(blockbottom_2_out_7), .c(blockbottom_2_out_8), .dp(blockbottom_2_out_16));
  BlockBottom blockbottom_2 (
    .out_13(blockbottom_2_out_13), .out_5(blockbottom_2_out_5), .out_6(blockbottom_2_out_6),
    .out_14(blockbottom_2_out_14), .out_15(blockbottom_2_out_15), .out_7(blockbottom_2_out_7),
    .out_8(blockbottom_2_out_8), .out_16(blockbottom_2_out_16), .out_17(blockbottom_2_out_17),
    .out_9(blockbottom_2_out_9), .out_10(blockbottom_2_out_10), .out_18(blockbottom_2_out_18),
    .out_19(blockbottom_2_out_19), .out_11(blockbottom_2_out_11), .out_12(blockbottom_2_out_12),
    .out_20(blockbottom_2_out_20), .in_1(Display_1[15:12]), .in_2(Display_1[11:8]), .in_3(Display_1[7:4]),
    .in_4(Display_1[3:0]));
  display u_display_1 (
    .sel(bitselector_1_out), .ctrl(disp), .Input_0(Data_1), .Output_0(Display_0), .Output_1(Display_1));
  BitSelector #(.width(16)) bitselector_1 (.in(IMM), .out(bitselector_1_out), .sel(4'b0000));
  BlockTop blocktop_2 (
    .in_1(Display_1[15:12]), .in_2(Display_1[11:8]), .in_3(Display_1[7:4]), .in_4(Display_1[3:0]),
    .out_5(blocktop_2_out_5), .out_13(blocktop_2_out_13), .out_14(blocktop_2_out_14),
    .out_6(blocktop_2_out_6), .out_7(blocktop_2_out_7), .out_15(blocktop_2_out_15),
    .out_16(blocktop_2_out_16), .out_8(blocktop_2_out_8), .out_9(blocktop_2_out_9),
    .out_17(blocktop_2_out_17), .out_18(blocktop_2_out_18), .out_10(blocktop_2_out_10),
    .out_11(blocktop_2_out_11), .out_19(blocktop_2_out_19), .out_20(blocktop_2_out_20),
    .out_12(blocktop_2_out_12));
  _7_Segment_Display u_7_segment_display_7 (
    .g(blocktop_2_out_11), .f(blocktop_2_out_19), .a(blocktop_2_out_20), .b(blocktop_2_out_12),
    .e(blockbottom_2_out_19), .d(blockbottom_2_out_11), .c(blockbottom_2_out_12), .dp(blockbottom_2_out_20));
  _7_Segment_Display u_7_segment_display_8 (
    .g(blocktop_2_out_9), .f(blocktop_2_out_17), .a(blocktop_2_out_18), .b(blocktop_2_out_10),
    .e(blockbottom_2_out_17), .d(blockbottom_2_out_9), .c(blockbottom_2_out_10), .dp(blockbottom_2_out_18));
  Multiplexer #(.width(16), .enable("false")) multiplexer_7 (
    .in0(Data_Mem_Addr), .in1(Data_Mem_Data), .out(multiplexer_7_out), .sel(MemtoReg));
  dec_inc_pc dec_inc_pc_3 (.dec_pc(br_PC), .dec_pc_2(dec_inc_pc_3_dec_pc_2));  // open: inc_pc, inc_pc_2
  Multiplexer #(.width(16), .enable("false")) multiplexer_8 (
    .in0(multiplexer_7_out), .in1(dec_inc_pc_3_dec_pc_2), .out(write_data), .sel(jal));

  // Other names for the same wires on the sheet: ALU_out[15:0] = Data_Mem_Addr; d0[15:0] = Display_0;
  //   d1[15:0] = Display_1; DMD[15:0] = Data_Mem_Data; FIM[15:0] = From_Instr_Mem; MemWrite = Data_Mem_Write;
  //   TIM[15:0] = To_Instr_Mem

  // Notes on the sheet:
  //   kill or not
  //   DECODE
  //   pc+1
  //   pc
  //   regfile
  //   if jal write to reg 3
  //   ALU
  //   DISPLAY[0]
  //   DISPLAY[1]
endmodule

module decode (
  input  [15:0] instruction,
  output [1:0] RS,
  output [1:0] RT,
  output [1:0] RD,
  output [5:0] FUNCT,
  output [7:0] IMMEDIATE,
  output [3:0] OPCODE,
  output [11:0] ADDR
);


  assign ADDR = instruction[11:0];
  assign FUNCT = instruction[5:0];
  assign IMMEDIATE = instruction[7:0];
  assign OPCODE = instruction[15:12];
  assign RD = instruction[7:6];
  assign RS = instruction[11:10];
  assign RT = instruction[9:8];

  // Notes on the sheet:
  //   breaks instruction into respective parts
endmodule

module Sign_Ext (
  input  [7:0] imm,
  input  [11:0] addr,
  input  in_3,
  output [15:0] se_addr,
  output [15:0] se_imm
);

  Multiplexer #(.width(16)) multiplexer_1 (
    .in0({4'b0000, addr}), .in1({{5{addr[11]}}, addr[10:0]}), .out(se_addr), .sel(in_3));  // open: en
  Multiplexer #(.width(16)) multiplexer_2 (
    .in0({{8{1'b0}}, imm}), .in1({{9{imm[7]}}, imm[6:0]}), .out(se_imm), .sel(in_3));  // open: en

  // Other names for the same wires on the sheet: s_u = in_3

  // Notes on the sheet:
  //   sign extends address field and immediate field
  //   if unsigned appends zero else sign extends
endmodule

module CONTROL (
  input  [3:0] opcode,
  output Display,
  output JAL,
  output JR,
  output BEQ,
  output Reg_Dest,
  output Branch,
  output Jump,
  output Extend,
  output Mem_reg,
  output Mem_write,
  output ALUSrc,
  output Reg_Write,
  output Rtype,
  output [3:0] ALU_op
);

  wire decoder_1_out2, decoder_1_out3, decoder_1_out4, decoder_1_out5, decoder_1_out7, decoder_1_out10;

  Decoder #(.select(4), .enable("false")) decoder_1 (
    .out0(Reg_Dest), .out1(Display), .out2(decoder_1_out2), .out3(decoder_1_out3), .out4(decoder_1_out4),
    .out5(decoder_1_out5), .out6(JAL), .out7(decoder_1_out7), .out8(JR), .out9(BEQ), .out10(decoder_1_out10),
    .out11(Mem_reg), .out12(Mem_write), .sel(opcode));  // open: out13, out14, out15
  or or_1 (Branch, BEQ, decoder_1_out10);
  or or_2 (Jump, JAL, decoder_1_out7, JR);
  or or_3 (Extend, decoder_1_out4, BEQ, decoder_1_out10, Mem_reg, Mem_write);
  or or_4 (ALUSrc, Mem_write, Mem_reg, decoder_1_out5, decoder_1_out4, decoder_1_out3, decoder_1_out2, Display);
  or or_5 (Reg_Write, Mem_reg, JAL, decoder_1_out5, decoder_1_out4, decoder_1_out3, decoder_1_out2, Reg_Dest);
  ALUOp_itype aluop_itype_1 (.ALU_op(ALU_op), .opcode(opcode));

  assign Rtype = Reg_Dest;

  // Notes on the sheet:
  //   Takes opcode determines what signals need to be propagated
  //   0:Rtype;  1:disp;  2:lui;  3:ori;  4:addi; 5 :andi; 6:jal: 7:j;  8:jr;  9:beq; 10:bne; 11:lw; 12:sw 
  //   *used for loads/store*
endmodule

module ALUOp_itype (
  input  [3:0] opcode,
  output [3:0] ALU_op
);

  Multiplexer #(.select(4), .width(4), .enable("false")) multiplexer_1 (
    .in0(4'b0000), .in1(4'b0000), .in2(4'b0100), .in3(4'b0000), .in4(4'b0010), .in5(4'b0001), .in6(4'b0000),
    .in7(4'b0000), .in8(4'b0000), .in9(4'b0011), .in10(4'b0011), .in11(4'b0010), .in12(4'b0010),
    .in13(4'b0000), .in14(4'b0000), .in15(4'b0000), .out(ALU_op), .sel(opcode));

  // Notes on the sheet:
  //   Given a particular I-type instruction finds the corresponding ALU operation required
  //   0=>OR; 1=>AND; 2=>ADD; 3=>SUB;
endmodule

module alu_switch (
  input  [3:0] I_type,
  input  [3:0] Rtype,
  input  R_flag,
  output [3:0] alu_switch
);

  Multiplexer #(.width(4), .enable("false")) multiplexer_1 (.in0(I_type), .in1(Rtype), .out(alu_switch), .sel(R_flag));

  // Notes on the sheet:
  //   Determines what type of function alu will execute
endmodule

module Branch (
  input  [15:0] pc,
  input  [15:0] imm,
  input  branch,
  input  equal,
  input  BEQ_BNE,
  output [15:0] pc_branch
);

  wire and_1_out, and_2_out, or_1_out;
  wire [15:0] adder_1_out, dec_inc_pc_1_dec_pc_2;

  and and_1 (and_1_out, branch, BEQ_BNE, equal);
  and and_2 (and_2_out, ~equal, ~BEQ_BNE, branch);  // AND_Gate
  dec_inc_pc dec_inc_pc_1 (.dec_pc(adder_1_out), .dec_pc_2(dec_inc_pc_1_dec_pc_2));  // open: inc_pc, inc_pc_2
  Adder #(.width(16)) adder_1 (.a(pc), .b(imm), .out(adder_1_out));  // open: cin, cout
  or or_1 (or_1_out, and_1_out, and_2_out);
  Multiplexer #(.width(16), .enable("false")) multiplexer_1 (
    .in0(pc), .in1(dec_inc_pc_1_dec_pc_2), .out(pc_branch), .sel(or_1_out));
endmodule

module dec_inc_pc (
  input  [15:0] inc_pc,
  input  [15:0] dec_pc,
  output [15:0] inc_pc_2,
  output [15:0] dec_pc_2
);

  Adder #(.width(16)) adder_1 (.a(inc_pc), .b(16'h1), .out(inc_pc_2));  // open: cin, cout
  Subtractor #(.width(16)) subtractor_1 (.a(dec_pc), .b(16'h1), .out(dec_pc_2));  // open: bin, bout

  // Notes on the sheet:
  //   decrements or incements 16 bit value 
  //   top=>inc || bottom=>dec
endmodule

module to_noop (
  input  beq,
  input  equal,
  input  branch,
  input  jr,
  input  jal,
  input  jump,
  output nop
);

  wire and_1_out, and_2_out;

  and and_1 (and_1_out, beq, equal, branch);
  and and_2 (and_2_out, ~equal, ~beq, branch);  // AND_Gate
  or or_1 (nop, and_1_out, and_2_out, jr, jal, jump);
endmodule

module display (
  input  sel,
  input  ctrl,
  input  [15:0] Input_0,
  output [15:0] Output_0,
  output [15:0] Output_1
);

  wire and_1_out, and_2_out, clk;

  Clock clock_1 (.out(clk));
  and and_1 (and_1_out, ~sel, ctrl);  // AND_Gate
  and and_2 (and_2_out, sel, ctrl);
  Register #(.width(16)) register_1 (.D(Input_0), .en(and_1_out), .Q(Output_0), .clk(clk));  // open: clr
  Register #(.width(16)) register_2 (.D(Input_0), .en(and_2_out), .Q(Output_1), .clk(clk));  // open: clr
endmodule
