// Logisim project hw6.circ as structural Verilog: 1 circuit, main circuit main
module main (
  input  _4_s_Place,
  input  _2_s_Place,
  input  _1_s_Place,
  output Output
);

  wire and_1_out, and_2_out, not_1_out, not_2_out, or_1_out;

  or or_1 (or_1_out, _2_s_Place, _4_s_Place);
  and and_1 (and_1_out, _1_s_Place, not_1_out);
  not not_1 (not_1_out, or_1_out);
  not not_2 (not_2_out, _1_s_Place);
  and and_2 (and_2_out, not_2_out, or_1_out);
  or or_2 (Output, and_1_out, and_2_out);
endmodule
