// Logisim project LAB10a.circ as structural Verilog: 6 circuits, main circuit main
module main (
  input  W,
  input  X,
  input  Y,
  input  Z,
  input  C0,
  input  C1,
  output out_7,
  output out_8,
  output out_9,
  output out_10,
  output O
);

  NAND NAND (.in_1(W), .in_2(X), .out_3(out_7));
  NOR nor_1 (.in_1(W), .in_2(X), .out_3(out_8));
  XOR XOR (.in_1(W), .in_2(X), .out_3(out_9));
  _2_to_1_MUX _2_to_1_MUX (.x(X), .y(W), .c0(C0), .o_p(out_10));
  _4_to_1_MUX _4_to_1_MUX (.x(W), .y(X), .z(Y), .w(Z), .c1(C0), .c0(C1), .o_p(O));

  // Notes on the sheet:
  //   NOR
endmodule

module NAND (
  input  in_1,
  input  in_2,
  output out_3
);

  wire and_1_out;

  and and_1 (and_1_out, in_1, in_2);
  not not_1 (out_3, and_1_out);
endmodule

module NOR (
  input  in_1,
  input  in_2,
  output out_3
);

  wire or_1_out;

  or or_1 (or_1_out, in_1, in_2);
  not not_1 (out_3, or_1_out);
endmodule

module XOR (
  input  in_1,
  input  in_2,
  output out_3
);

  wire and_1_out, and_2_out, not_1_out, not_2_out;

  not not_1 (not_1_out, in_1);
  not not_2 (not_2_out, in_2);
  and and_1 (and_1_out, not_1_out, in_2);
  and and_2 (and_2_out, not_2_out, in_1);
  or or_1 (out_3, and_1_out, and_2_out);
endmodule

module _2_to_1_MUX (
  input  x,
  input  y,
  input  c0,
  output o_p
);

  wire and_1_out, and_2_out, not_1_out;

  not not_1 (not_1_out, c0);
  and and_1 (and_1_out, x, not_1_out);
  and and_2 (and_2_out, y, c0);
  XOR xor_1 (.in_1(and_1_out), .in_2(and_2_out), .out_3(o_p));
endmodule

module _4_to_1_MUX (
  input  x,
  input  y,
  input  z,
  input  w,
  input  c1,
  input  c0,
  output o_p
);

  wire n2_to_1_mux_1_o_p, n2_to_1_mux_2_o_p;

  _2_to_1_MUX u_2_to_1_mux_1 (.x(x), .y(y), .c0(c1), .o_p(n2_to_1_mux_1_o_p));
  _2_to_1_MUX u_2_to_1_mux_2 (.x(z), .y(w), .c0(c1), .o_p(n2_to_1_mux_2_o_p));
  _2_to_1_MUX u_2_to_1_mux_3 (.x(n2_to_1_mux_1_o_p), .y(n2_to_1_mux_2_o_p), .c0(c0), .o_p(o_p));
endmodule
