// Logisim project lab11.circ as structural Verilog: 26 circuits, main circuit main
module add_to_inf (
  input  clk,
  input  Stop,
  output [15:0] n,
  output [15:0] n_1,
  output [15:0] o_p
);

  wire register_1_q;
  wire [15:0] multiplexer_1_out;

  Multiplexer #(.width(16), .enable("false")) multiplexer_1 (
    .in0(16'h1), .in1(o_p), .out(multiplexer_1_out), .sel(register_1_q));
  Register #(.width(1)) register_1 (.D(1'b1), .Q(register_1_q), .clk(clk));  // open: en, clr
  Register #(.width(16)) u_n (.D(multiplexer_1_out), .en(Stop), .Q(n), .clk(clk));  // open: clr
  Register #(.width(16)) u_n_1 (.D(n), .en(Stop), .Q(n_1), .clk(clk));  // open: clr
  Adder #(.width(16)) adder_1 (.a(n), .b(n_1), .out(o_p));  // open: cin, cout

  // Other names for the same wires on the sheet: o_p_n_1[15:0] = n_1; o_p_of_add[15:0] = o_p
endmodule

module inputFib (
  input  [15:0] Current_State,
  output [15:0] \output ,
  output [15:0] Next_State_1,
  output [15:0] Next_State_2
);

  wire and_1_out, and_2_out, comparator_1_eq, comparator_2_eq, comparator_2_gt;
  wire [15:0] multiplexer_3_out;

  Comparator #(.width(16)) comparator_1 (.a(Current_State), .b({16{1'b0}}), .eq(comparator_1_eq));  // open: gt, lt
  Comparator #(.width(16)) comparator_2 (
    .a(Current_State), .b(16'h1), .gt(comparator_2_gt), .eq(comparator_2_eq));  // open: lt
  Multiplexer #(.width(16)) multiplexer_1 (.in0({16{1'b0}}), .out(\output ), .sel(1'b0), .en(and_1_out));  // open: in1
  and and_1 (and_1_out, comparator_1_eq, 1'b1);
  and and_2 (and_2_out, comparator_2_eq, 1'b1);
  Multiplexer #(.width(16)) multiplexer_2 (.in0(16'h1), .out(\output ), .sel(1'b0), .en(and_2_out));  // open: in1
  Multiplexer #(.width(16)) multiplexer_3 (
    .in0(Current_State), .out(multiplexer_3_out), .sel(1'b0), .en(comparator_2_gt));  // open: in1
  sub1 n_1 (.in_1(multiplexer_3_out), .out_2(Next_State_1));
  Sub2 n_2 (.in_1(multiplexer_3_out), .out_2(Next_State_2));
endmodule

module Fib (
  output [15:0] out_1
);

  wire Clk, comparator_1_eq, comparator_2_eq, not_1_out;
  wire [7:0] stop;
  wire [15:0] multiplexer_1_out, register_1_q, register_2_q, register_3_q;

  Comparator comparator_1 (.a(8'hf), .b(stop), .eq(comparator_1_eq));  // open: gt, lt
  Multiplexer #(.width(16), .enable("false")) multiplexer_1 (
    .in0(out_1), .in1(16'h1), .out(multiplexer_1_out), .sel(comparator_2_eq));
  Comparator #(.width(16)) comparator_2 (.a({16{1'b0}}), .b(out_1), .eq(comparator_2_eq));  // open: gt, lt
  not not_1 (not_1_out, comparator_1_eq);
  Register #(.width(16)) register_1 (.D(multiplexer_1_out), .en(not_1_out), .Q(register_1_q), .clk(Clk));  // open: clr
  Register #(.width(16)) register_2 (.D(register_1_q), .en(not_1_out), .Q(register_2_q), .clk(Clk));  // open: clr
  Register #(.width(16)) register_3 (.D(out_1), .en(not_1_out), .Q(register_3_q), .clk(Clk));  // open: clr
  Clock clock_1 (.out(Clk));
  Hex_Digit_Display hex_digit_display_1 (.value(out_1[15:12]));  // open: dp
  Adder #(.width(16)) adder_1 (.a(register_2_q), .b(register_3_q), .out(out_1));  // open: cin, cout
  Hex_Digit_Display hex_digit_display_2 (.value(out_1[11:8]));  // open: dp
  Hex_Digit_Display hex_digit_display_3 (.value(out_1[7:4]));  // open: dp
  // Probe on out_1
  Hex_Digit_Display hex_digit_display_4 (.value(out_1[3:0]));  // open: dp
  Counter counter_1 (.count(not_1_out), .Q(stop), .clk(Clk));  // open: load, D, carry, clr
  Hex_Digit_Display hex_digit_display_5 (.value(stop[7:4]));  // open: dp
  Hex_Digit_Display hex_digit_display_6 (.value(stop[3:0]));  // open: dp
  // Probe on stop

  // Other names for the same wires on the sheet: count[15:0] = out_1
endmodule

module If_1 (
  input  [15:0] in_1
);
endmodule

module counter (
  input  in_1,
  input  in_2,
  output [3:0] out_3,
  output [3:0] out_4
);

  Adder #(.width(4)) adder_1 (.a(4'b0001), .b(out_4), .out(out_3));  // open: cin, cout
  Register #(.width(4)) register_1 (.D(out_3), .en(in_2), .Q(out_4), .clk(in_1));  // open: clr

  // Other names for the same wires on the sheet: Clk = in_1; R = in_2
endmodule

module Sub2 (
  input  [15:0] in_1,
  output [15:0] out_2
);

  wire [15:0] sub1_1_out_2;

  sub1 sub1_1 (.in_1(in_1), .out_2(sub1_1_out_2));
  sub1 sub1_2 (.in_1(sub1_1_out_2), .out_2(out_2));
endmodule

module sub1 (
  input  [15:0] in_1,
  output [15:0] out_2
);

  Subtractor #(.width(16)) subtractor_1 (.a(in_1), .b(16'h1), .out(out_2));  // open: bin, bout
endmodule

module main (
  input  [15:0] Input,
  input  [3:0] in_2,
  output [15:0] out_3,
  output [15:0] Output
);

  rotrB rotrb (.in_1(Input), .in_2(in_2), .out_3(out_3));
  rotr rotr (.in_1(Input), .in_2(in_2), .out_3(Output));
endmodule

module Ex1 (
  input  [7:0] Input,
  output Out1,
  output [7:0] Out2
);

  wire [5:0] not_2_out;
  wire [7:0] not_1_out;

  and and_1 (Out1, Input[0], Input[7]);
  not not_1 (not_1_out[0], Input[0]);
  assign not_2_out = ~Input[6:1];  // NOT_Gate not_2, 6 bits wide
  not not_3 (not_1_out[7], Input[7]);
  Adder adder_1 (.a({not_1_out[7], not_2_out, not_1_out[0]}), .b(8'h1), .out(Out2));  // open: cin, cout
endmodule

module rotr (
  input  [15:0] in_1,
  input  [3:0] in_2,
  output [15:0] out_3
);

  wire [15:0] a_1_1_out_2, a_2_1_out_2, a_3_1_out_2, a_4_1_out_2, a_5_1_out_2, a_6_1_out_2, a_7_1_out_2,
       a_8_1_out_2, a_9_1_out_2, a_10_1_out_2, a_11_1_out_2, a_12_1_out_2, a_13_1_out_2, a_14_1_out_2,
       a_15_1_out_2;

  A____1 a_1_1 (.in_1(in_1), .out_2(a_1_1_out_2));
  A____2 a_2_1 (.in_1(in_1), .out_2(a_2_1_out_2));
  A____3 a_3_1 (.in_1(in_1), .out_2(a_3_1_out_2));
  A____4 a_4_1 (.in_1(in_1), .out_2(a_4_1_out_2));
  A____5 a_5_1 (.in_1(in_1), .out_2(a_5_1_out_2));
  A____6 a_6_1 (.in_1(in_1), .out_2(a_6_1_out_2));
  A____7 a_7_1 (.in_1(in_1), .out_2(a_7_1_out_2));
  A____8 a_8_1 (.in_1(in_1), .out_2(a_8_1_out_2));
  A____9 a_9_1 (.in_1(in_1), .out_2(a_9_1_out_2));
  A____10 a_10_1 (.in_1(in_1), .out_2(a_10_1_out_2));
  A____11 a_11_1 (.in_1(in_1), .out_2(a_11_1_out_2));
  A____12 a_12_1 (.in_1(in_1), .out_2(a_12_1_out_2));
  A____13 a_13_1 (.in_1(in_1), .out_2(a_13_1_out_2));
  A____14 a_14_1 (.in_1(in_1), .out_2(a_14_1_out_2));
  A____15 a_15_1 (.in_1(in_1), .out_2(a_15_1_out_2));
  Multiplexer #(.select(4), .width(16), .enable("false")) multiplexer_1 (
    .in0(in_1), .in1(a_1_1_out_2), .in2(a_2_1_out_2), .in3(a_3_1_out_2), .in4(a_4_1_out_2),
    .in5(a_5_1_out_2), .in6(a_6_1_out_2), .in7(a_7_1_out_2), .in8(a_8_1_out_2), .in9(a_9_1_out_2),
    .in10(a_10_1_out_2), .in11(a_11_1_out_2), .in12(a_12_1_out_2), .in13(a_13_1_out_2), .in14(a_14_1_out_2),
    .in15(a_15_1_out_2), .out(out_3), .sel(in_2));
endmodule

module A____1 (
  input  [15:0] in_1,
  output [15:0] out_2
);


  assign out_2 = {in_1[0], in_1[15:1]};
endmodule

module A____2 (
  input  [15:0] in_1,
  output [15:0] out_2
);

  wire [15:0] a_1_1_out_2;

  A____1 a_1_1 (.in_1(in_1), .out_2(a_1_1_out_2));
  A____1 a_1_2 (.in_1(a_1_1_out_2), .out_2(out_2));
endmodule

module A____3 (
  input  [15:0] in_1,
  output [15:0] out_2
);

  wire [15:0] a_2_1_out_2;

  A____2 a_2_1 (.in_1(in_1), .out_2(a_2_1_out_2));
  A____1 a_1_1 (.in_1(a_2_1_out_2), .out_2(out_2));
endmodule

module A____4 (
  input  [15:0] in_1,
  output [15:0] out_2
);

  wire [15:0] a_2_1_out_2;

  A____2 a_2_1 (.in_1(in_1), .out_2(a_2_1_out_2));
  A____2 a_2_2 (.in_1(a_2_1_out_2), .out_2(out_2));
endmodule

module A____5 (
  input  [15:0] in_1,
  output [15:0] out_2
);

  wire [15:0] a_4_1_out_2;

  A____4 a_4_1 (.in_1(in_1), .out_2(a_4_1_out_2));
  A____1 a_1_1 (.in_1(a_4_1_out_2), .out_2(out_2));
endmodule

module A____6 (
  input  [15:0] in_1,
  output [15:0] out_2
);

  wire [15:0] a_3_1_out_2;

  A____3 a_3_1 (.in_1(in_1), .out_2(a_3_1_out_2));
  A____3 a_3_2 (.in_1(a_3_1_out_2), .out_2(out_2));
endmodule

module A____7 (
  input  [15:0] in_1,
  output [15:0] out_2
);

  wire [15:0] a_3_1_out_2;

  A____3 a_3_1 (.in_1(in_1), .out_2(a_3_1_out_2));
  A____4 a_4_1 (.in_1(a_3_1_out_2), .out_2(out_2));
endmodule

module A____8 (
  input  [15:0] in_1,
  output [15:0] out_2
);

  wire [15:0] a_4_1_out_2;

  A____4 a_4_1 (.in_1(in_1), .out_2(a_4_1_out_2));
  A____4 a_4_2 (.in_1(a_4_1_out_2), .out_2(out_2));
endmodule

module A____10 (
  input  [15:0] in_1,
  output [15:0] out_2
);

  wire [15:0] a_5_1_out_2;

  A____5 a_5_1 (.in_1(in_1), .out_2(a_5_1_out_2));
  A____5 a_5_2 (.in_1(a_5_1_out_2), .out_2(out_2));
endmodule

module A____11 (
  input  [15:0] in_1,
  output [15:0] out_2
);

  wire [15:0] a_6_1_out_2;

  A____6 a_6_1 (.in_1(in_1), .out_2(a_6_1_out_2));
  A____5 a_5_1 (.in_1(a_6_1_out_2), .out_2(out_2));
endmodule

module A____12 (
  input  [15:0] in_1,
  output [15:0] out_2
);

  wire [15:0] a_6_1_out_2;

  A____6 a_6_1 (.in_1(in_1), .out_2(a_6_1_out_2));
  A____6 a_6_2 (.in_1(a_6_1_out_2), .out_2(out_2));
endmodule

module A____13 (
  input  [15:0] in_1,
  output [15:0] out_2
);

  wire [15:0] a_6_1_out_2;

  A____6 a_6_1 (.in_1(in_1), .out_2(a_6_1_out_2));
  A____7 a_7_1 (.in_1(a_6_1_out_2), .out_2(out_2));
endmodule

module A____14 (
  input  [15:0] in_1,
  output [15:0] out_2
);

  wire [15:0] a_7_1_out_2;

  A____7 a_7_1 (.in_1(in_1), .out_2(a_7_1_out_2));
  A____7 a_7_2 (.in_1(a_7_1_out_2), .out_2(out_2));
endmodule

module A____15 (
  input  [15:0] in_1,
  output [15:0] out_2
);

  wire [15:0] a_14_1_out_2;

  A____14 a_14_1 (.in_1(in_1), .out_2(a_14_1_out_2));
  A____1 a_1_1 (.in_1(a_14_1_out_2), .out_2(out_2));
endmodule

module A____9 (
  input  [15:0] in_1,
  output [15:0] out_2
);

  wire [15:0] a_4_1_out_2;

  A____5 a_5_1 (.in_1(a_4_1_out_2), .out_2(out_2));
  A____4 a_4_1 (.in_1(in_1), .out_2(a_4_1_out_2));
endmodule

module rotrB (
  input  [15:0] in_1,
  input  [3:0] in_2,
  output [15:0] out_3
);

  wire not_1_out, not_2_out, not_3_out, not_4_out;
  wire [15:0] a_1_1_out_2, a_2_1_out_2, a_4_1_out_2, a_8_1_out_2, multiplexer_1_out, multiplexer_2_out,
       multiplexer_3_out;

  A____8 a_8_1 (.in_1(in_1), .out_2(a_8_1_out_2));
  not not_1 (not_1_out, in_2[3]);
  Multiplexer #(.width(16), .enable("false")) multiplexer_1 (
    .in0(a_8_1_out_2), .in1(in_1), .out(multiplexer_1_out), .sel(not_1_out));
  A____4 a_4_1 (.in_1(multiplexer_1_out), .out_2(a_4_1_out_2));
  not not_2 (not_2_out, in_2[2]);
  A____2 a_2_1 (.in_1(multiplexer_2_out), .out_2(a_2_1_out_2));
  Multiplexer #(.width(16), .enable("false")) multiplexer_2 (
    .in0(a_4_1_out_2), .in1(multiplexer_1_out), .out(multiplexer_2_out), .sel(not_2_out));
  not not_3 (not_3_out, in_2[1]);
  not not_4 (not_4_out, in_2[0]);
  Multiplexer #(.width(16), .enable("false")) multiplexer_3 (
    .in0(a_2_1_out_2), .in1(multiplexer_2_out), .out(multiplexer_3_out), .sel(not_3_out));
  A____1 a_1_1 (.in_1(multiplexer_3_out), .out_2(a_1_1_out_2));
  Multiplexer #(.width(16), .enable("false")) multiplexer_4 (
    .in0(a_1_1_out_2), .in1(multiplexer_3_out), .out(out_3), .sel(not_4_out));
endmodule
