// Logisim project alu.circ as structural Verilog
module main (
  input  [15:0] X,
  input  [15:0] Y,
  input  [3:0] switch__S,
  output signed_overflow,
  output [15:0] result,
  output equal
);

  wire comparator_1_eq, comparator_2_eq, control, signedOF;
  wire [15:0] operations_1_add, operations_1_and, operations_1_bc, operations_1_ffo, operations_1_lui,
       operations_1_or, operations_1_sllv, operations_1_slt, operations_1_srav, operations_1_srlv,
       operations_1_sub, operations_1_zb;

  Comparator #(.width(4)) comparator_1 (.a(4'b0110), .b(switch__S), .eq(comparator_1_eq));  // open: gt, lt
  Comparator #(.width(4)) comparator_2 (.a(4'b0111), .b(switch__S), .eq(comparator_2_eq));  // open: gt, lt
  Operations operations_1 (
    .X(X), .Y(Y), .\or (operations_1_or), .\and (operations_1_and), .slt(operations_1_slt),
    .srlv(operations_1_srlv), .sllv(operations_1_sllv), .srav(operations_1_srav), .add(operations_1_add),
    .sub(operations_1_sub), .bc(operations_1_bc), .zb(operations_1_zb), .ffo(operations_1_ffo),
    .signed_overflow(signedOF), .equal(equal), .lui(operations_1_lui));
  or or_1 (control, comparator_1_eq, comparator_2_eq);
  Multiplexer #(.enable("false")) multiplexer_1 (.in0(1'b0), .in1(signedOF), .out(signed_overflow), .sel(control));
  Multiplexer #(.select(4), .width(16), .enable("false")) multiplexer_2 (
    .in0(operations_1_and), .in1(operations_1_or), .in2(operations_1_slt), .in3(operations_1_sllv),
    .in4(operations_1_srlv), .in5(operations_1_srav), .in6(operations_1_add), .in7(operations_1_sub),
    .in8(operations_1_bc), .in9(operations_1_zb), .in10(operations_1_ffo), .in11(operations_1_lui),
    .out(result), .sel(switch__S));  // open: in12, in13, in14, in15

  // Other names for the same wires on the sheet: isequal = equal

  // Notes on the sheet:
  //   UNSIGNED OVERFLOW?
  //   SIGNED OVERFLOW?
endmodule

module ffo (
  input  [15:0] X,
  output [15:0] out
);

  wire [3:0] bitfinder_1_index;
  wire [15:0] bit_extender_1_out;

  BitFinder #(.width(16), .\type ("high1")) bitfinder_1 (.in(X), .index(bitfinder_1_index));  // open: found
  assign bit_extender_1_out = {{12{1'b0}}, bitfinder_1_index};  // Bit_Extender bit_extender_1
  Subtractor #(.width(16)) subtractor_1 (.a(16'hf), .b(bit_extender_1_out), .out(out));  // open: bin, bout
endmodule

module srav (
  input  [15:0] X,
  input  [15:0] Y,
  output [15:0] out
);

  wire [3:0] bit_extender_1_out;

  Shifter #(.width(15)) shifter_1 (.in(X[14:0]), .\dist (bit_extender_1_out), .out(out[14:0]));
  Bit_Extender #(.in_width(16), .out_width(4)) bit_extender_1 (.in(Y), .out(bit_extender_1_out));

  assign out[15] = X[15];
endmodule

module zb (
  input  [15:0] X,
  output [15:0] out
);

  wire comparator_1_eq, comparator_2_eq, comparator_3_eq, comparator_4_eq, comparator_5_eq, comparator_6_eq,
       comparator_7_eq, comparator_8_eq, comparator_9_eq, comparator_10_eq, or_1_out;

  Comparator comparator_1 (.a(X[7:0]), .b({8{1'b0}}), .eq(comparator_1_eq));  // open: gt, lt
  Comparator comparator_2 (.a(X[15:8]), .b({8{1'b0}}), .eq(comparator_2_eq));  // open: gt, lt
  Comparator comparator_3 (.a(X[14:7]), .b({8{1'b0}}), .eq(comparator_3_eq));  // open: gt, lt
  Comparator comparator_4 (.a(X[13:6]), .b({8{1'b0}}), .eq(comparator_4_eq));  // open: gt, lt
  Comparator comparator_5 (.a(X[12:5]), .b({8{1'b0}}), .eq(comparator_5_eq));  // open: gt, lt
  Comparator comparator_6 (.a(X[11:4]), .b({8{1'b0}}), .eq(comparator_6_eq));  // open: gt, lt
  Comparator comparator_7 (.a(X[11:4]), .b({8{1'b0}}), .eq(comparator_7_eq));  // open: gt, lt
  Comparator comparator_8 (.a(X[10:3]), .b({8{1'b0}}), .eq(comparator_8_eq));  // open: gt, lt
  Comparator comparator_9 (.a(X[9:2]), .b({8{1'b0}}), .eq(comparator_9_eq));  // open: gt, lt
  Comparator comparator_10 (.a(X[8:1]), .b({8{1'b0}}), .eq(comparator_10_eq));  // open: gt, lt
  or or_1 (or_1_out, comparator_1_eq, comparator_2_eq, comparator_3_eq, comparator_4_eq, comparator_5_eq, comparator_6_eq, comparator_7_eq, comparator_8_eq, comparator_9_eq, comparator_10_eq);
  assign out = {{15{1'b0}}, or_1_out};  // Bit_Extender bit_extender_1
endmodule

module bc (
  input  [15:0] X,
  output [15:0] out
);

  wire [4:0] bitadder_1_out;

  BitAdder #(.width(16)) bitadder_1 (.in0(X), .out(bitadder_1_out));
  assign out = {{11{1'b0}}, bitadder_1_out};  // Bit_Extender bit_extender_1
endmodule

module Operations (
  input  [15:0] X,
  input  [15:0] Y,
  output [15:0] \or ,
  output [15:0] \and ,
  output [15:0] slt,
  output [15:0] srlv,
  output [15:0] sllv,
  output [15:0] srav,
  output [15:0] add,
  output [15:0] sub,
  output [15:0] bc,
  output [15:0] zb,
  output [15:0] ffo,
  output signed_overflow,
  output equal,
  output [15:0] lui
);

  wire comparator_1_lt;
  wire [3:0] bit_extender_1_out, bit_extender_2_out;

  Bit_Extender #(.in_width(16), .out_width(4)) bit_extender_1 (.in(Y), .out(bit_extender_1_out));
  Bit_Extender #(.in_width(16), .out_width(4)) bit_extender_2 (.in(Y), .out(bit_extender_2_out));
  assign \or  = X | Y;  // OR_Gate or_1, 16 bits wide
  assign \and  = X & Y;  // AND_Gate and_1, 16 bits wide
  Comparator #(.width(16)) comparator_1 (.a(X), .b(Y), .eq(equal), .lt(comparator_1_lt));  // open: gt
  Shifter #(.width(16), .shift("lr")) shifter_1 (.in(X), .\dist (bit_extender_1_out), .out(srlv));
  Shifter #(.width(16)) shifter_2 (.in(X), .\dist (bit_extender_2_out), .out(sllv));
  srav srav_1 (.X(X), .Y(Y), .out(srav));
  Adder #(.width(16)) adder_1 (.a(X), .b(Y), .out(add));  // open: cin, cout
  Subtractor #(.width(16)) subtractor_1 (.a(X), .b(Y), .out(sub));  // open: bin, bout
  bc u_bc (.X(X), .out(bc));
  zb u_zb (.X(X), .out(zb));
  ffo u_ffo (.X(X), .out(ffo));
  sign_overflow sign_overflow_1 (
    .A_sig(Y[15]), .B_sig(X[15]), .Sum_sig(add[15]), .Sub_sig(sub[15]), .Sum_OF(signed_overflow));
  Shifter #(.width(16)) shifter_3 (.in(Y), .\dist (4'b1000), .out(lui));
  assign slt = {{15{1'b0}}, comparator_1_lt};  // Bit_Extender bit_extender_3

  // Other names for the same wires on the sheet: addo_p[15:0] = add; isequal = equal; sub_o_p[15:0] = sub
endmodule

module sign_overflow (
  input  A_sig,
  input  B_sig,
  input  Sum_sig,
  input  Sub_sig,
  output Sum_OF
);

  wire and_1_out, and_2_out, and_3_out, and_4_out, or_1_out, or_2_out;

  and and_1 (and_1_out, ~A_sig, ~B_sig, Sum_sig);  // AND_Gate
  and and_2 (and_2_out, A_sig, B_sig, ~Sum_sig);  // AND_Gate
  and and_3 (and_3_out, A_sig, ~B_sig, ~Sub_sig);  // AND_Gate
  and and_4 (and_4_out, ~A_sig, B_sig, Sub_sig);  // AND_Gate
  or or_1 (or_1_out, and_1_out, and_2_out);
  or or_2 (or_2_out, and_3_out, and_4_out);
  or or_3 (Sum_OF, or_1_out, or_2_out);
endmodule

module add (
  input  [15:0] in_1,
  input  [15:0] in_2,
  output out_3,
  output [15:0] out_4,
  output unsigned_OF
);

  wire bitselector_1_out, bitselector_2_out, bitselector_3_out;

  BitSelector #(.width(16)) bitselector_1 (.in(in_1), .out(bitselector_1_out), .sel(4'b1111));
  BitSelector #(.width(16)) bitselector_2 (.in(in_2), .out(bitselector_2_out), .sel(4'b1111));
  BitSelector #(.width(16)) bitselector_3 (.in(out_4), .out(bitselector_3_out), .sel(4'b1111));

  // Notes on the sheet:
  //   sigbit
endmodule
