// Logisim project cpu.circ as structural Verilog
module main (
  input  [15:0] From_Instr_Mem,
  input  clk,
  output [15:0] r0,
  output [15:0] r1,
  output [15:0] r2,
  output [15:0] r3,
  output [15:0] Display_0,
  output [15:0] Display_1,
  output [15:0] To_Instr_Mem,
  output [15:0] Data_Mem_Data,
  output [15:0] Data_Mem_Addr,
  output Data_Mem_Write
);

  cpunew_main main_1 (
    .From_Instr_Mem(From_Instr_Mem), .To_Instr_Mem(To_Instr_Mem), .Data_Mem_Data(Data_Mem_Data),
    .Data_Mem_Addr(Data_Mem_Addr), .Data_Mem_Write(Data_Mem_Write), .r0(r0), .r1(r1), .r2(r2), .r3(r3),
    .Display_0(Display_0), .Display_1(Display_1), .clk(clk));

  // Other names for the same wires on the sheet: d0[15:0] = Display_0; d1[15:0] = Display_1

  // Notes on the sheet:
  //   This is a CLK that is an INPUT driven from the harness.
  //   Remember, this circuit is loaded from the harness to be tested!
  //   These are OUTPUTS to the circuit
  //   DO NOT CHANGE THE LOCATIONS OF THE INPUTS/OUTPUTS! IF YOU DO SO, YOU NEED TO MAKE SURE THE PINS ARE AT THE RIGHT PLACE!
  //   These are OUTPUTS to the circuit
endmodule

module Display_Out (
  input  [15:0] \input ,
  input  input_overflow,
  input  enable,
  output [3:0] out_4,
  output [3:0] out_5,
  output [3:0] out_6,
  output [3:0] out_7,
  output [15:0] Display_Out,
  output output_overflow
);

  wire controlled_buffer_3_out, not_1_out, not_2_out;
  wire [15:0] controlled_buffer_1_out;

  not not_1 (not_1_out, enable);
  assign controlled_buffer_1_out = not_1_out ? {16{1'b0}} : 16'bz;  // Controlled_Buffer controlled_buffer_1
  assign controlled_buffer_1_out = enable ? Display_Out : 16'bz;  // Controlled_Buffer controlled_buffer_2
  Multiplexer #(.width(16), .enable("false")) multiplexer_1 (
    .in0(controlled_buffer_1_out), .in1(\input ), .out(Display_Out), .sel(enable));
  not not_2 (not_2_out, enable);
  assign controlled_buffer_3_out = not_2_out ? 1'b0 : 1'bz;  // Controlled_Buffer controlled_buffer_3
  assign controlled_buffer_3_out = enable ? output_overflow : 1'bz;  // Controlled_Buffer controlled_buffer_4
  Multiplexer #(.enable("false")) multiplexer_2 (
    .in0(controlled_buffer_3_out), .in1(input_overflow), .out(output_overflow), .sel(enable));

  assign out_4 = Display_Out[15:12];
  assign out_5 = Display_Out[11:8];
  assign out_6 = Display_Out[7:4];
  assign out_7 = Display_Out[3:0];
endmodule

module Instr_Sel (
  input  [15:0] From_Instr_Mem,
  output [1:0] rs,
  output [1:0] rt,
  output [1:0] rd,
  output [5:0] func,
  output [3:0] opcode,
  output [15:0] Zero_ext_imm_off,
  output [15:0] Sign_ext_imm_off,
  output [15:0] Target_Address,
  output isFunc,
  output RegWrite
);

  wire comparator_1_lt, comparator_2_eq, op_equal_1_op_8, op_equal_1_op_9, op_equal_1_op_10,
       op_equal_1_op_11, op_equal_1_op_15;

  op_equal op_equal_1 (
    .opcode(From_Instr_Mem[15:12]), .op_8(op_equal_1_op_8), .op_9(op_equal_1_op_9), .op_10(op_equal_1_op_10),
    .op_11(op_equal_1_op_11), .op_15(op_equal_1_op_15));  // open: op_0, op_1, op_2, op_3, op_4, op_5, op_6, op_7, op_12, op_13, op_14
  nor nor_1 (RegWrite, op_equal_1_op_8, op_equal_1_op_9, op_equal_1_op_10, op_equal_1_op_11, op_equal_1_op_15);
  assign Zero_ext_imm_off = {{8{1'b0}}, From_Instr_Mem[7:0]};  // Bit_Extender bit_extender_1
  assign Sign_ext_imm_off = {{8{From_Instr_Mem[7]}}, From_Instr_Mem[7:0]};  // Bit_Extender bit_extender_2
  assign Target_Address = {{4{1'b0}}, From_Instr_Mem[11:0]};  // Bit_Extender bit_extender_3
  Comparator #(.width(6)) comparator_1 (.a(From_Instr_Mem[5:0]), .b(6'b001000), .lt(comparator_1_lt));  // open: gt, eq
  Comparator #(.width(4)) comparator_2 (.a(From_Instr_Mem[15:12]), .b(4'b0000), .eq(comparator_2_eq));  // open: gt, lt
  and and_1 (isFunc, comparator_1_lt, comparator_2_eq);

  assign func = From_Instr_Mem[5:0];
  assign opcode = From_Instr_Mem[15:12];
  assign rd = From_Instr_Mem[7:6];
  assign rs = From_Instr_Mem[11:10];
  assign rt = From_Instr_Mem[9:8];

  // Other names for the same wires on the sheet: func1[5:0] = From_Instr_Mem[5:0];
  //   immediate_offset[7:0] = From_Instr_Mem[7:0]; target_address_t[11:0] = From_Instr_Mem[11:0];
  //   opcode1[3:0] = From_Instr_Mem[15:12]
endmodule

module Mem (
  input  [15:0] Data_In,
  input  [15:0] Address,
  input  Reset,
  input  clk,
  input  RegWrite,
  output [15:0] Data_Out
);

  wire not_1_out;

  assign Data_Out = RegWrite ? Data_In : 16'bz;  // Controlled_Buffer controlled_buffer_1
  RAM #(.addrWidth(16), .dataWidth(16)) ram_1 (
    .addr(Address), .data(Data_Out), .sel(1'b1), .clk(clk), .ld(not_1_out), .clr(Reset));
  not not_1 (not_1_out, RegWrite);
endmodule

module op_equal (
  input  [3:0] opcode,
  output op_0,
  output op_1,
  output op_2,
  output op_3,
  output op_4,
  output op_5,
  output op_6,
  output op_7,
  output op_8,
  output op_9,
  output op_10,
  output op_11,
  output op_12,
  output op_13,
  output op_14,
  output op_15
);

  Comparator #(.width(4), .mode("unsigned")) comparator_1 (.a(4'b0000), .b(opcode), .eq(op_0));  // open: gt, lt
  Comparator #(.width(4), .mode("unsigned")) comparator_2 (.a(4'b0001), .b(opcode), .eq(op_1));  // open: gt, lt
  Comparator #(.width(4), .mode("unsigned")) comparator_3 (.a(4'b0010), .b(opcode), .eq(op_2));  // open: gt, lt
  Comparator #(.width(4), .mode("unsigned")) comparator_4 (.a(4'b0011), .b(opcode), .eq(op_3));  // open: gt, lt
  Comparator #(.width(4), .mode("unsigned")) comparator_5 (.a(4'b0100), .b(opcode), .eq(op_4));  // open: gt, lt
  Comparator #(.width(4), .mode("unsigned")) comparator_6 (.a(4'b0101), .b(opcode), .eq(op_5));  // open: gt, lt
  Comparator #(.width(4), .mode("unsigned")) comparator_7 (.a(4'b0110), .b(opcode), .eq(op_6));  // open: gt, lt
  Comparator #(.width(4), .mode("unsigned")) comparator_8 (.a(4'b0111), .b(opcode), .eq(op_7));  // open: gt, lt
  Comparator #(.width(4), .mode("unsigned")) comparator_9 (.a(4'b1000), .b(opcode), .eq(op_8));  // open: gt, lt
  Comparator #(.width(4), .mode("unsigned")) comparator_10 (.a(4'b1001), .b(opcode), .eq(op_9));  // open: gt, lt
  Comparator #(.width(4), .mode("unsigned")) comparator_11 (.a(4'b1010), .b(opcode), .eq(op_10));  // open: gt, lt
  Comparator #(.width(4), .mode("unsigned")) comparator_12 (.a(4'b1011), .b(opcode), .eq(op_11));  // open: gt, lt
  Comparator #(.width(4), .mode("unsigned")) comparator_13 (.a(4'b1100), .b(opcode), .eq(op_12));  // open: gt, lt
  Comparator #(.width(4), .mode("unsigned")) comparator_14 (.a(4'b1101), .b(opcode), .eq(op_13));  // open: gt, lt
  Comparator #(.width(4), .mode("unsigned")) comparator_15 (.a(4'b1110), .b(opcode), .eq(op_14));  // open: gt, lt
  Comparator #(.width(4), .mode("unsigned")) comparator_16 (.a(4'b1111), .b(opcode), .eq(op_15));  // open: gt, lt
endmodule

module PC_Counter (
  input  [15:0] imm,
  input  clk,
  input  reset,
  input  [15:0] Target_Address,
  input  [15:0] rs,
  input  [3:0] opcode,
  output [15:0] new_PC
);

  wire op_equal_1_op_7, op_equal_1_op_8, op_equal_1_op_10, op_equal_1_op_11;
  wire [2:0] or_3_out;
  wire [15:0] adder_1_out, adder_2_out, and_1_out, multiplexer_1_out, or_1_out;

  Adder #(.width(16)) adder_1 (.a(16'h1), .b(new_PC), .out(adder_1_out));  // open: cin, cout
  assign and_1_out = new_PC & 16'hf000;  // AND_Gate and_1, 16 bits wide
  Adder #(.width(16)) adder_2 (.a(imm), .b(adder_1_out), .out(adder_2_out));  // open: cin, cout
  assign or_1_out = and_1_out | Target_Address;  // OR_Gate or_1, 16 bits wide
  or or_2 (or_3_out[1], op_equal_1_op_7, op_equal_1_op_8);
  op_equal op_equal_1 (
    .opcode(opcode), .op_7(op_equal_1_op_7), .op_8(op_equal_1_op_8), .op_9(or_3_out[2]),
    .op_10(op_equal_1_op_10), .op_11(op_equal_1_op_11));  // open: op_0, op_1, op_2, op_3, op_4, op_5, op_6, op_12, op_13, op_14, op_15
  Multiplexer #(.select(3), .width(16), .enable("false")) multiplexer_1 (
    .in0(adder_2_out), .in1(adder_1_out), .in2(or_1_out), .in4(rs), .out(multiplexer_1_out), .sel(or_3_out));  // open: in3, in5, in6, in7
  or or_3 (or_3_out[0], op_equal_1_op_10, op_equal_1_op_11);
  Register #(.width(16)) register_1 (.D(multiplexer_1_out), .Q(new_PC), .clk(clk), .clr(reset));  // open: en
endmodule

module Write_Register (
  input  [1:0] rd,
  input  [1:0] rt,
  input  [3:0] opcode,
  output [1:0] Reg2Write
);

  Multiplexer #(.select(4), .width(2), .enable("false")) multiplexer_1 (
    .in0(rd), .in1(rt), .in2(rt), .in3(rt), .in4(rt), .in5(rt), .in6(rt), .in7(2'b11), .in13(rt), .in14(rt),
    .out(Reg2Write), .sel(opcode));  // open: in8, in9, in10, in11, in12, in15

  // Notes on the sheet:
  //   $r3
endmodule

module Read_Register (
  input  [1:0] rs,
  input  [3:0] opcode,
  input  [1:0] rt,
  output [1:0] Read_Reg_1,
  output [1:0] Read_Reg_2
);

  Multiplexer #(.select(4), .width(2), .enable("false")) multiplexer_1 (
    .in0(rs), .in1(rs), .in2(rs), .in3(rs), .in4(rs), .in5(rs), .in6(rs), .in9(rs), .in10(rs), .in11(rs),
    .in12(rt), .in14(rs), .in15(rs), .out(Read_Reg_1), .sel(opcode));  // open: in7, in8, in13
  Multiplexer #(.select(4), .width(2), .enable("false")) multiplexer_2 (
    .in0(rt), .in10(rt), .in11(rt), .out(Read_Reg_2), .sel(opcode));  // open: in1, in2, in3, in4, in5, in6, in7, in8, in9, in12, in13, in14, in15
endmodule

module ALU_Source (
  input  [15:0] rt,
  input  [15:0] rs,
  input  [3:0] opcode,
  input  [15:0] unsign_imm,
  input  [15:0] sign_imm,
  output [15:0] X,
  output [15:0] Y
);

  wire [1:0] multiplexer_6_out, multiplexer_7_out;
  wire [15:0] multiplexer_1_out, multiplexer_2_out, multiplexer_3_out;

  Multiplexer #(.select(4), .width(16), .enable("false")) multiplexer_1 (
    .in0(rt), .in4(rt), .in10(rt), .in11(rt), .in12(rt), .in13(16'h8), .out(multiplexer_1_out), .sel(opcode));  // open: in1, in2, in3, in5, in6, in7, in8, in9, in14, in15
  Multiplexer #(.select(4), .width(16), .enable("false")) multiplexer_2 (
    .in0(rs), .in1(rs), .in2(rs), .in3(rs), .in4(rs), .in5(rs), .in6(rs), .in9(rs), .in10(rs), .in11(rs),
    .in12(rs), .in14(rs), .in15(rs), .out(multiplexer_2_out), .sel(opcode));  // open: in7, in8, in13
  Multiplexer #(.select(4), .width(16), .enable("false")) multiplexer_3 (
    .in1(unsign_imm), .in2(unsign_imm), .in3(unsign_imm), .in4(sign_imm), .in5(unsign_imm), .in6(unsign_imm),
    .in10(sign_imm), .in11(sign_imm), .in12(sign_imm), .in13(unsign_imm), .in14(sign_imm), .in15(unsign_imm),
    .out(multiplexer_3_out), .sel(opcode));  // open: in0, in7, in8, in9
  Multiplexer #(.select(2), .width(16), .enable("false")) multiplexer_4 (
    .in0(multiplexer_3_out), .in1(multiplexer_2_out), .in2(multiplexer_1_out), .out(X),
    .sel(multiplexer_6_out));  // open: in3
  Multiplexer #(.select(2), .width(16), .enable("false")) multiplexer_5 (
    .in0(multiplexer_3_out), .in1(multiplexer_1_out), .in2(multiplexer_2_out), .out(Y),
    .sel(multiplexer_7_out));  // open: in3
  Multiplexer #(.select(4), .width(2), .enable("false")) multiplexer_6 (
    .in0(2'b01), .in1(2'b01), .in2(2'b01), .in3(2'b01), .in4(2'b10), .in5(2'b01), .in6(2'b01), .in10(2'b01),
    .in11(2'b01), .in12(2'b01), .in13(2'b00), .in14(2'b01), .in15(2'b01), .out(multiplexer_6_out),
    .sel(opcode));  // open: in7, in8, in9
  Multiplexer #(.select(4), .width(2), .enable("false")) multiplexer_7 (
    .in0(2'b10), .in3(2'b00), .in4(2'b00), .in5(2'b00), .in6(2'b00), .in10(2'b01), .in11(2'b01),
    .in12(2'b00), .in13(2'b01), .in14(2'b00), .in15(2'b00), .out(multiplexer_7_out), .sel(opcode));  // open: in1, in2, in7, in8, in9
endmodule

module ALU_ctr_signal (
  input  [5:0] func,
  input  isFunc,
  input  [3:0] opcode,
  output [3:0] switch_S
);

  wire [5:0] multiplexer_1_out, multiplexer_2_out;

  Multiplexer #(.select(4), .width(6), .enable("false")) multiplexer_1 (
    .in4(6'b000110), .in5({6{1'b0}}), .in6(6'b000001), .in10(6'b001011), .in11(6'b001011), .in12(6'b000001),
    .in13(6'b000011), .in14(6'b000001), .out(multiplexer_1_out), .sel(opcode));  // open: in0, in1, in2, in3, in7, in8, in9, in15
  Multiplexer #(.width(6), .enable("false")) multiplexer_2 (
    .in0(multiplexer_1_out), .in1(func), .out(multiplexer_2_out), .sel(isFunc));
  Bit_Extender #(.in_width(6), .out_width(4)) bit_extender_1 (.in(multiplexer_2_out), .out(switch_S));
endmodule

module Mem_to_Write (
  input  [3:0] opcode,
  input  clk,
  output Mem_Write,
  output lui,
  output lw,
  output ReadMem
);

  wire [3:0] register_1_q;

  Register #(.width(4)) register_1 (.D(opcode), .Q(register_1_q), .clk(clk));  // open: en, clr
  op_equal op_equal_1 (
    .opcode(register_1_q), .op_12(Mem_Write), .op_13(lui), .op_14(lw));  // open: op_0, op_1, op_2, op_3, op_4, op_5, op_6, op_7, op_8, op_9, op_10, op_11, op_15
  or or_1 (ReadMem, lui, lw);
endmodule

module Display_Enable (
  input  [3:0] opcode,
  input  [15:0] un_imm,
  output D0,
  output D1
);

  wire bit_extender_1_out, comparator_1_eq;

  Demultiplexer #(.enable("false")) demultiplexer_1 (
    .out0(D0), .out1(D1), .in(comparator_1_eq), .sel(bit_extender_1_out));
  Comparator #(.width(4)) comparator_1 (.a(opcode), .b(4'b1111), .eq(comparator_1_eq));  // open: gt, lt
  Bit_Extender #(.in_width(16), .out_width(1)) bit_extender_1 (.in(un_imm), .out(bit_extender_1_out));
endmodule
