// Logisim project cpunew.circ as structural Verilog
module main (
  input  [15:0] From_Instr_Mem,
  input  clk,
  output [15:0] r0,
  output [15:0] r1,
  output [15:0] r2,
  output [15:0] r3,
  output [15:0] Display_0,
  output [15:0] Display_1,
  output [15:0] To_Instr_Mem,
  output [15:0] Data_Mem_Data,
  output [15:0] Data_Mem_Addr,
  output Data_Mem_Write
);

  cpu cpu_1 (
    .From_Instr_Mem(From_Instr_Mem), .To_Instr_Mem(To_Instr_Mem), .Data_Mem_Data(Data_Mem_Data),
    .Data_Mem_Addr(Data_Mem_Addr), .Data_Mem_Write(Data_Mem_Write), .r0(r0), .r1(r1), .r2(r2), .r3(r3),
    .Display_0(Display_0), .Display_1(Display_1), .clk(clk));

  // Other names for the same wires on the sheet: d0[15:0] = Display_0; d1[15:0] = Display_1

  // Notes on the sheet:
  //   This is a CLK that is an INPUT driven from the harness.
  //   Remember, this circuit is loaded from the harness to be tested!
  //   These are OUTPUTS to the circuit
  //   DO NOT CHANGE THE LOCATIONS OF THE INPUTS/OUTPUTS! IF YOU DO SO, YOU NEED TO MAKE SURE THE PINS ARE AT THE RIGHT PLACE!
  //   These are OUTPUTS to the circuit
endmodule

module Display_Out (
  input  [15:0] \input ,
  input  input_overflow,
  input  enable,
  output [3:0] out_4,
  output [3:0] out_5,
  output [3:0] out_6,
  output [3:0] out_7,
  output [15:0] Display_Out,
  output output_overflow
);

  wire controlled_buffer_3_out, not_1_out, not_2_out;
  wire [15:0] controlled_buffer_1_out;

  not not_1 (not_1_out, enable);
  assign controlled_buffer_1_out = not_1_out ? {16{1'b0}} : 16'bz;  // Controlled_Buffer controlled_buffer_1
  assign controlled_buffer_1_out = enable ? Display_Out : 16'bz;  // Controlled_Buffer controlled_buffer_2
  Multiplexer #(.width(16), .enable("false")) multiplexer_1 (
    .in0(controlled_buffer_1_out), .in1(\input ), .out(Display_Out), .sel(enable));
  not not_2 (not_2_out, enable);
  assign controlled_buffer_3_out = not_2_out ? 1'b0 : 1'bz;  // Controlled_Buffer controlled_buffer_3
  assign controlled_buffer_3_out = enable ? output_overflow : 1'bz;  // Controlled_Buffer controlled_buffer_4
  Multiplexer #(.enable("false")) multiplexer_2 (
    .in0(controlled_buffer_3_out), .in1(input_overflow), .out(output_overflow), .sel(enable));

  assign out_4 = Display_Out[15:12];
  assign out_5 = Display_Out[11:8];
  assign out_6 = Display_Out[7:4];
  assign out_7 = Display_Out[3:0];
endmodule

module Instr_Sel (
  input  [15:0] From_Instr_Mem,
  output [1:0] rs,
  output [1:0] rt,
  output [1:0] rd,
  output [5:0] func,
  output [3:0] opcode,
  output [15:0] Zero_ext_imm_off,
  output [15:0] Sign_ext_imm_off,
  output [15:0] Target_Address,
  output isFunc,
  output RegWrite
);

  wire comparator_1_lt, comparator_2_eq, op_equal_1_op_8, op_equal_1_op_9, op_equal_1_op_10,
       op_equal_1_op_11, op_equal_1_op_15;

  op_equal op_equal_1 (
    .opcode(From_Instr_Mem[15:12]), .op_8(op_equal_1_op_8), .op_9(op_equal_1_op_9), .op_10(op_equal_1_op_10),
    .op_11(op_equal_1_op_11), .op_15(op_equal_1_op_15));  // open: op_0, op_1, op_2, op_3, op_4, op_5, op_6, op_7, op_12, op_13, op_14
  nor nor_1 (RegWrite, op_equal_1_op_8, op_equal_1_op_9, op_equal_1_op_10, op_equal_1_op_11, op_equal_1_op_15);
  assign Zero_ext_imm_off = {{8{1'b0}}, From_Instr_Mem[7:0]};  // Bit_Extender bit_extender_1
  assign Sign_ext_imm_off = {{8{From_Instr_Mem[7]}}, From_Instr_Mem[7:0]};  // Bit_Extender bit_extender_2
  assign Target_Address = {{4{1'b0}}, From_Instr_Mem[11:0]};  // Bit_Extender bit_extender_3
  Comparator #(.width(6)) comparator_1 (.a(From_Instr_Mem[5:0]), .b(6'b001000), .lt(comparator_1_lt));  // open: gt, eq
  Comparator #(.width(4)) comparator_2 (.a(From_Instr_Mem[15:12]), .b(4'b0000), .eq(comparator_2_eq));  // open: gt, lt
  and and_1 (isFunc, comparator_1_lt, comparator_2_eq);

  assign func = From_Instr_Mem[5:0];
  assign opcode = From_Instr_Mem[15:12];
  assign rd = From_Instr_Mem[7:6];
  assign rs = From_Instr_Mem[11:10];
  assign rt = From_Instr_Mem[9:8];

  // Other names for the same wires on the sheet: func1[5:0] = From_Instr_Mem[5:0];
  //   immediate_offset[7:0] = From_Instr_Mem[7:0]; target_address_t[11:0] = From_Instr_Mem[11:0];
  //   opcode1[3:0] = From_Instr_Mem[15:12]
endmodule

module Mem (
  input  [15:0] Data_In,
  input  [15:0] Address,
  input  Reset,
  input  clk,
  input  RegWrite,
  output [15:0] Data_Out
);

  wire not_1_out;

  assign Data_Out = RegWrite ? Data_In : 16'bz;  // Controlled_Buffer controlled_buffer_1
  RAM #(.addrWidth(16), .dataWidth(16)) ram_1 (
    .addr(Address), .data(Data_Out), .sel(1'b1), .clk(clk), .ld(not_1_out), .clr(Reset));
  not not_1 (not_1_out, RegWrite);
endmodule

module op_equal (
  input  [3:0] opcode,
  output op_0,
  output op_1,
  output op_2,
  output op_3,
  output op_4,
  output op_5,
  output op_6,
  output op_7,
  output op_8,
  output op_9,
  output op_10,
  output op_11,
  output op_12,
  output op_13,
  output op_14,
  output op_15
);

  Comparator #(.width(4), .mode("unsigned")) comparator_1 (.a(4'b0000), .b(opcode), .eq(op_0));  // open: gt, lt
  Comparator #(.width(4), .mode("unsigned")) comparator_2 (.a(4'b0001), .b(opcode), .eq(op_1));  // open: gt, lt
  Comparator #(.width(4), .mode("unsigned")) comparator_3 (.a(4'b0010), .b(opcode), .eq(op_2));  // open: gt, lt
  Comparator #(.width(4), .mode("unsigned")) comparator_4 (.a(4'b0011), .b(opcode), .eq(op_3));  // open: gt, lt
  Comparator #(.width(4), .mode("unsigned")) comparator_5 (.a(4'b0100), .b(opcode), .eq(op_4));  // open: gt, lt
  Comparator #(.width(4), .mode("unsigned")) comparator_6 (.a(4'b0101), .b(opcode), .eq(op_5));  // open: gt, lt
  Comparator #(.width(4), .mode("unsigned")) comparator_7 (.a(4'b0110), .b(opcode), .eq(op_6));  // open: gt, lt
  Comparator #(.width(4), .mode("unsigned")) comparator_8 (.a(4'b0111), .b(opcode), .eq(op_7));  // open: gt, lt
  Comparator #(.width(4), .mode("unsigned")) comparator_9 (.a(4'b1000), .b(opcode), .eq(op_8));  // open: gt, lt
  Comparator #(.width(4), .mode("unsigned")) comparator_10 (.a(4'b1001), .b(opcode), .eq(op_9));  // open: gt, lt
  Comparator #(.width(4), .mode("unsigned")) comparator_11 (.a(4'b1010), .b(opcode), .eq(op_10));  // open: gt, lt
  Comparator #(.width(4), .mode("unsigned")) comparator_12 (.a(4'b1011), .b(opcode), .eq(op_11));  // open: gt, lt
  Comparator #(.width(4), .mode("unsigned")) comparator_13 (.a(4'b1100), .b(opcode), .eq(op_12));  // open: gt, lt
  Comparator #(.width(4), .mode("unsigned")) comparator_14 (.a(4'b1101), .b(opcode), .eq(op_13));  // open: gt, lt
  Comparator #(.width(4), .mode("unsigned")) comparator_15 (.a(4'b1110), .b(opcode), .eq(op_14));  // open: gt, lt
  Comparator #(.width(4), .mode("unsigned")) comparator_16 (.a(4'b1111), .b(opcode), .eq(op_15));  // open: gt, lt
endmodule

module PC_Counter (
  input  [15:0] imm,
  input  clk,
  input  reset,
  input  [15:0] Target_Address,
  input  [15:0] rs,
  input  [3:0] opcode,
  output [15:0] new_PC
);

  wire op_equal_1_op_7, op_equal_1_op_8, op_equal_1_op_10, op_equal_1_op_11;
  wire [2:0] or_3_out;
  wire [15:0] adder_1_out, adder_2_out, and_1_out, multiplexer_1_out, or_1_out;

  Adder #(.width(16)) adder_1 (.a(16'h1), .b(new_PC), .out(adder_1_out));  // open: cin, cout
  assign and_1_out = new_PC & 16'hf000;  // AND_Gate and_1, 16 bits wide
  Adder #(.width(16)) adder_2 (.a(imm), .b(adder_1_out), .out(adder_2_out));  // open: cin, cout
  assign or_1_out = and_1_out | Target_Address;  // OR_Gate or_1, 16 bits wide
  or or_2 (or_3_out[1], op_equal_1_op_7, op_equal_1_op_8);
  op_equal op_equal_1 (
    .opcode(opcode), .op_7(op_equal_1_op_7), .op_8(op_equal_1_op_8), .op_9(or_3_out[2]),
    .op_10(op_equal_1_op_10), .op_11(op_equal_1_op_11));  // open: op_0, op_1, op_2, op_3, op_4, op_5, op_6, op_12, op_13, op_14, op_15
  Multiplexer #(.select(3), .width(16), .enable("false")) multiplexer_1 (
    .in0(adder_2_out), .in1(adder_1_out), .in2(or_1_out), .in4(rs), .out(multiplexer_1_out), .sel(or_3_out));  // open: in3, in5, in6, in7
  or or_3 (or_3_out[0], op_equal_1_op_10, op_equal_1_op_11);
  Register #(.width(16)) register_1 (.D(multiplexer_1_out), .Q(new_PC), .clk(clk), .clr(reset));  // open: en
endmodule

module Write_Register (
  input  [1:0] rd,
  input  [1:0] rt,
  input  [3:0] opcode,
  output [1:0] Reg2Write
);

  Multiplexer #(.select(4), .width(2), .enable("false")) multiplexer_1 (
    .in0(rd), .in1(rt), .in2(rt), .in3(rt), .in4(rt), .in5(rt), .in6(rt), .in7(2'b11), .in13(rt), .in14(rt),
    .out(Reg2Write), .sel(opcode));  // open: in8, in9, in10, in11, in12, in15

  // Notes on the sheet:
  //   $r3
endmodule

module Read_Register (
  input  [1:0] rs,
  input  [3:0] opcode,
  input  [1:0] rt,
  output [1:0] Read_Reg_1,
  output [1:0] Read_Reg_2
);

  Multiplexer #(.select(4), .width(2), .enable("false")) multiplexer_1 (
    .in0(rs), .in1(rs), .in2(rs), .in3(rs), .in4(rs), .in5(rs), .in6(rs), .in9(rs), .in10(rs), .in11(rs),
    .in12(rt), .in14(rs), .in15(rs), .out(Read_Reg_1), .sel(opcode));  // open: in7, in8, in13
  Multiplexer #(.select(4), .width(2), .enable("false")) multiplexer_2 (
    .in0(rt), .in10(rt), .in11(rt), .out(Read_Reg_2), .sel(opcode));  // open: in1, in2, in3, in4, in5, in6, in7, in8, in9, in12, in13, in14, in15
endmodule

module ALU_Source (
  input  [15:0] rt,
  input  [15:0] rs,
  input  [3:0] opcode,
  input  [15:0] unsign_imm,
  input  [15:0] sign_imm,
  output [15:0] X,
  output [15:0] Y
);

  wire [1:0] multiplexer_6_out, multiplexer_7_out;
  wire [15:0] multiplexer_1_out, multiplexer_2_out, multiplexer_3_out;

  Multiplexer #(.select(4), .width(16), .enable("false")) multiplexer_1 (
    .in0(rt), .in4(rt), .in10(rt), .in11(rt), .in12(rt), .in13(16'h8), .out(multiplexer_1_out), .sel(opcode));  // open: in1, in2, in3, in5, in6, in7, in8, in9, in14, in15
  Multiplexer #(.select(4), .width(16), .enable("false")) multiplexer_2 (
    .in0(rs), .in1(rs), .in2(rs), .in3(rs), .in4(rs), .in5(rs), .in6(rs), .in9(rs), .in10(rs), .in11(rs),
    .in12(rs), .in14(rs), .in15(rs), .out(multiplexer_2_out), .sel(opcode));  // open: in7, in8, in13
  Multiplexer #(.select(4), .width(16), .enable("false")) multiplexer_3 (
    .in1(unsign_imm), .in2(unsign_imm), .in3(unsign_imm), .in4(sign_imm), .in5(unsign_imm), .in6(unsign_imm),
    .in10(sign_imm), .in11(sign_imm), .in12(sign_imm), .in13(unsign_imm), .in14(sign_imm), .in15(unsign_imm),
    .out(multiplexer_3_out), .sel(opcode));  // open: in0, in7, in8, in9
  Multiplexer #(.select(2), .width(16), .enable("false")) multiplexer_4 (
    .in0(multiplexer_3_out), .in1(multiplexer_2_out), .in2(multiplexer_1_out), .out(X),
    .sel(multiplexer_6_out));  // open: in3
  Multiplexer #(.select(2), .width(16), .enable("false")) multiplexer_5 (
    .in0(multiplexer_3_out), .in1(multiplexer_1_out), .in2(multiplexer_2_out), .out(Y),
    .sel(multiplexer_7_out));  // open: in3
  Multiplexer #(.select(4), .width(2), .enable("false")) multiplexer_6 (
    .in0(2'b01), .in1(2'b01), .in2(2'b01), .in3(2'b01), .in4(2'b10), .in5(2'b01), .in6(2'b01), .in10(2'b01),
    .in11(2'b01), .in12(2'b01), .in13(2'b00), .in14(2'b01), .in15(2'b01), .out(multiplexer_6_out),
    .sel(opcode));  // open: in7, in8, in9
  Multiplexer #(.select(4), .width(2), .enable("false")) multiplexer_7 (
    .in0(2'b10), .in3(2'b00), .in4(2'b00), .in5(2'b00), .in6(2'b00), .in10(2'b01), .in11(2'b01),
    .in12(2'b00), .in13(2'b01), .in14(2'b00), .in15(2'b00), .out(multiplexer_7_out), .sel(opcode));  // open: in1, in2, in7, in8, in9
endmodule

module ALU_ctr_signal (
  input  [5:0] func,
  input  isFunc,
  input  [3:0] opcode,
  output [3:0] switch_S
);

  wire [5:0] multiplexer_1_out, multiplexer_2_out;

  Multiplexer #(.select(4), .width(6), .enable("false")) multiplexer_1 (
    .in4(6'b000110), .in5({6{1'b0}}), .in6(6'b000001), .in10(6'b001011), .in11(6'b001011), .in12(6'b000001),
    .in13(6'b000011), .in14(6'b000001), .out(multiplexer_1_out), .sel(opcode));  // open: in0, in1, in2, in3, in7, in8, in9, in15
  Multiplexer #(.width(6), .enable("false")) multiplexer_2 (
    .in0(multiplexer_1_out), .in1(func), .out(multiplexer_2_out), .sel(isFunc));
  Bit_Extender #(.in_width(6), .out_width(4)) bit_extender_1 (.in(multiplexer_2_out), .out(switch_S));
endmodule

module Mem_to_Write (
  input  [3:0] opcode,
  input  clk,
  output Mem_Write,
  output lui,
  output lw,
  output ReadMem
);

  wire [3:0] register_1_q;

  Register #(.width(4)) register_1 (.D(opcode), .Q(register_1_q), .clk(clk));  // open: en, clr
  op_equal op_equal_1 (
    .opcode(register_1_q), .op_12(Mem_Write), .op_13(lui), .op_14(lw));  // open: op_0, op_1, op_2, op_3, op_4, op_5, op_6, op_7, op_8, op_9, op_10, op_11, op_15
  or or_1 (ReadMem, lui, lw);
endmodule

module Display_Enable (
  input  [3:0] opcode,
  input  [15:0] un_imm,
  output D0,
  output D1
);

  wire bit_extender_1_out, comparator_1_eq;

  Demultiplexer #(.enable("false")) demultiplexer_1 (
    .out0(D0), .out1(D1), .in(comparator_1_eq), .sel(bit_extender_1_out));
  Comparator #(.width(4)) comparator_1 (.a(opcode), .b(4'b1111), .eq(comparator_1_eq));  // open: gt, lt
  Bit_Extender #(.in_width(16), .out_width(1)) bit_extender_1 (.in(un_imm), .out(bit_extender_1_out));
endmodule

module display (
  input  sel,
  input  ctrl,
  input  [15:0] Input_0,
  output [15:0] Output_0,
  output [15:0] Output_1
);

  wire and_1_out, and_2_out, clk;

  Clock clock_1 (.out(clk));
  and and_1 (and_1_out, ~sel, ctrl);  // AND_Gate
  and and_2 (and_2_out, sel, ctrl);
  Register #(.width(16)) register_1 (.D(Input_0), .en(and_1_out), .Q(Output_0), .clk(clk));  // open: clr
  Register #(.width(16)) register_2 (.D(Input_0), .en(and_2_out), .Q(Output_1), .clk(clk));  // open: clr
endmodule

module control (
  input  [3:0] opcode,
  output JAL,
  output JR,
  output BEQ,
  output Display,
  output Reg_Dest,
  output Branch,
  output Jump,
  output Extend,
  output Mem_reg,
  output Mem_write,
  output ALUSrc,
  output Reg_Write,
  output Rtype,
  output [3:0] ALU_op
);

  wire decoder_1_out1, decoder_1_out2, decoder_1_out3, decoder_1_out4, decoder_1_out5, decoder_1_out6,
       decoder_1_out8, decoder_1_out11, decoder_1_out13;

  Decoder #(.select(4), .enable("false")) decoder_1 (
    .out0(Reg_Dest), .out1(decoder_1_out1), .out2(decoder_1_out2), .out3(decoder_1_out3),
    .out4(decoder_1_out4), .out5(decoder_1_out5), .out6(decoder_1_out6), .out7(JAL), .out8(decoder_1_out8),
    .out9(JR), .out10(BEQ), .out11(decoder_1_out11), .out12(Mem_write), .out13(decoder_1_out13),
    .out14(Mem_reg), .out15(Display), .sel(opcode));
  or or_1 (Branch, decoder_1_out11, BEQ);
  or or_2 (Jump, JAL, decoder_1_out8, JR);
  or or_3 (Extend, Mem_reg, Mem_write, decoder_1_out11, BEQ, decoder_1_out4);
  or or_4 (ALUSrc, Display, Mem_reg, decoder_1_out13, Mem_write, decoder_1_out6, decoder_1_out5, decoder_1_out4, decoder_1_out3, decoder_1_out2, decoder_1_out1);
  or or_5 (Reg_Write, Mem_reg, decoder_1_out13, JAL, decoder_1_out6, decoder_1_out5, decoder_1_out4, decoder_1_out3, decoder_1_out2, decoder_1_out1, Reg_Dest);
  ALUOp_itype aluop_itype_1 (.ALU_op(ALU_op), .opcode(opcode));

  assign Rtype = Reg_Dest;

  // Notes on the sheet:
  //   Takes opcode determines what signals need to be propagated
  //   *used for loads/store*
endmodule

module ALUOp_itype (
  input  [3:0] opcode,
  output [3:0] ALU_op
);

  Multiplexer #(.select(4), .width(4), .enable("false")) multiplexer_1 (
    .in0(4'b0000), .in1(4'b1010), .in2(4'b1001), .in3(4'b1000), .in4(4'b0110), .in5(4'b0000), .in6(4'b0001),
    .in7(4'b0000), .in8(4'b0000), .in9(4'b0000), .in10(4'b0111), .in11(4'b0111), .in12(4'b0110),
    .in13(4'b1011), .in14(4'b0110), .in15(4'b0000), .out(ALU_op), .sel(opcode));

  // Notes on the sheet:
  //   Given a particular I-type instruction finds the corresponding ALU operation required
  //   0=>AND; 1=>OR; 3=>SLLV; 6 =>ADD; 7=>SUB; 8=>BC; 9=>ZB; 10=>FFO
endmodule

module dec_inc_pc (
  input  [15:0] inc_pc,
  input  [15:0] dec_pc,
  output [15:0] inc_pc_2,
  output [15:0] dec_pc_2
);

  Adder #(.width(16)) adder_1 (.a(inc_pc), .b(16'h1), .out(inc_pc_2));  // open: cin, cout
  Subtractor #(.width(16)) subtractor_1 (.a(dec_pc), .b(16'h1), .out(dec_pc_2));  // open: bin, bout

  // Notes on the sheet:
  //   decrements or incements 16 bit value 
  //   top=>inc || bottom=>dec
endmodule

module cpu (
  input  [15:0] From_Instr_Mem,
  input  clk,
  output [15:0] r0,
  output [15:0] r1,
  output [15:0] r2,
  output [15:0] r3,
  output [15:0] Display_0,
  output [15:0] Display_1,
  output [15:0] To_Instr_Mem,
  output [15:0] Data_Mem_Data,
  output [15:0] Data_Mem_Addr,
  output Data_Mem_Write
);

  wire ALUSrc, beq, bitselector_1_out, Branch, disp, equal, jal, jr, Jump, MemRead, MemtoReg, no_op,
       not_1_out, overflow, R_type, Reg_Dest, RegWrite;
  wire [1:0] multiplexer_2_out, multiplexer_4_out, RD, RS, RT;
  wire [3:0] alu_sw_1_alu_switch, ALUOp, bit_extender_1_out, opcode;
  wire [5:0] funct;
  wire [7:0] decode_of_cpu_1_immediate;
  wire [11:0] decode_of_cpu_1_addr;
  wire [15:0] ADDR, and_1_out, br_PC, Data_1, Data_2, dec_inc_pc_1_inc_pc_2, dec_inc_pc_2_dec_pc_2,
       dec_inc_pc_3_dec_pc_2, IMM, multiplexer_1_out, multiplexer_3_out, multiplexer_5_out,
       multiplexer_6_out, multiplexer_7_out, or_1_out, register_1_q, write_data;

  // Probe on multiplexer_1_out
  Multiplexer #(.width(16), .enable("false")) multiplexer_1 (
    .in0(From_Instr_Mem), .in1({16{1'b0}}), .out(multiplexer_1_out), .sel(no_op));
  Register #(.width(16)) register_1 (.D(multiplexer_1_out), .en(1'b1), .Q(register_1_q), .clk(clk));  // open: clr
  decode_of_cpu decode_of_cpu_1 (
    .instruction(register_1_q), .RS(RS), .RT(RT), .RD(RD), .FUNCT(funct),
    .IMMEDIATE(decode_of_cpu_1_immediate), .ADDR(decode_of_cpu_1_addr), .OPCODE(opcode));
  No_Op no_op_1 (.beq(beq), .equal(equal), .branch(Branch), .jr(jr), .jal(jal), .jump(Jump), .nop(no_op));
  Sign_Extend sign_extend_1 (
    .imm(decode_of_cpu_1_immediate), .addr(decode_of_cpu_1_addr), .in_3(MemRead), .se_addr(IMM), .se_imm(ADDR));
  // Probe on multiplexer_3_out
  Register #(.width(16)) register_2 (.D(multiplexer_3_out), .en(1'b1), .Q(To_Instr_Mem), .clk(clk));  // open: clr
  dec_inc_pc dec_inc_pc_1 (.inc_pc(To_Instr_Mem), .inc_pc_2(dec_inc_pc_1_inc_pc_2));  // open: dec_pc, dec_pc_2
  dec_inc_pc dec_inc_pc_2 (.dec_pc(To_Instr_Mem), .dec_pc_2(dec_inc_pc_2_dec_pc_2));  // open: inc_pc, inc_pc_2
  // Probe on multiplexer_2_out
  Multiplexer #(.width(2), .enable("false")) multiplexer_2 (
    .in0(RT), .in1(RD), .out(multiplexer_2_out), .sel(Reg_Dest));
  Multiplexer #(.width(16), .enable("false")) multiplexer_3 (
    .in0(multiplexer_5_out), .in1(Data_1), .out(multiplexer_3_out), .sel(jr));
  Branch branch_1 (
    .pc(dec_inc_pc_1_inc_pc_2), .imm(IMM), .branch(Branch), .equal(equal), .BEQ_BNE(beq), .pc_branch(br_PC));
  assign and_1_out = dec_inc_pc_2_dec_pc_2 & 16'hf000;  // AND_Gate and_1, 16 bits wide
  Multiplexer #(.width(2), .enable("false")) multiplexer_4 (
    .in0(multiplexer_2_out), .in1(2'b11), .out(multiplexer_4_out), .sel(jal));
  assign or_1_out = and_1_out | ADDR;  // OR_Gate or_1, 16 bits wide
  Multiplexer #(.width(16), .enable("false")) multiplexer_5 (
    .in0(br_PC), .in1(or_1_out), .out(multiplexer_5_out), .sel(Jump));
  // Probe on Data_2
  Regfile_main main_1 (
    .Read_register_1(RS), .Read_register_2(RT), .write_register(multiplexer_4_out), .write_data(write_data),
    .Read_Data_1(Data_1), .Read_Data_2(Data_2), .Reg_0_Value(r0), .Reg_1_Value(r1), .Reg_2_Value(r2),
    .Reg_3_Value(r3), .RegWrite(RegWrite), .clock(clk));
  // Probe on Data_1
  // Probe on IMM
  // Probe on bit_extender_1_out
  Bit_Extender #(.in_width(6), .out_width(4)) bit_extender_1 (.in(funct), .out(bit_extender_1_out));
  // Probe on ALUOp
  control control_1 (
    .opcode(opcode), .Reg_Dest(Reg_Dest), .Branch(Branch), .Jump(Jump), .Extend(MemRead), .Mem_reg(MemtoReg),
    .Mem_write(Data_Mem_Write), .ALUSrc(ALUSrc), .Reg_Write(RegWrite), .Rtype(R_type), .ALU_op(ALUOp),
    .Display(disp), .JAL(jal), .JR(jr), .BEQ(beq));
  // Probe on multiplexer_6_out
  alu_main main_2 (
    .switch__S(alu_sw_1_alu_switch), .X(Data_1), .equal(equal), .result(Data_Mem_Addr),
    .signed_overflow(overflow), .Y(multiplexer_6_out));
  Multiplexer #(.width(16), .enable("false")) multiplexer_6 (
    .in0(Data_2), .in1(IMM), .out(multiplexer_6_out), .sel(ALUSrc));
  ALU_SW alu_sw_1 (.I_type(ALUOp), .Rtype(bit_extender_1_out), .alu_switch(alu_sw_1_alu_switch), .R_flag(R_type));
  // Probe on Data_Mem_Addr
  // Probe on alu_sw_1_alu_switch
  Hex_Digit_Display hex_digit_display_1 (.value(Display_0[11:8]));  // open: dp
  Hex_Digit_Display hex_digit_display_2 (.value(Display_0[15:12]));  // open: dp
  assign Data_Mem_Data = Data_Mem_Write ? Data_2 : 16'bz;  // Controlled_Buffer controlled_buffer_1
  not not_1 (not_1_out, Data_Mem_Write);
  Hex_Digit_Display hex_digit_display_3 (.value(Display_0[7:4]));  // open: dp
  Hex_Digit_Display hex_digit_display_4 (.value(Display_0[3:0]));  // open: dp
  RAM #(.addrWidth(16), .dataWidth(16)) ram_1 (
    .addr(Data_Mem_Addr), .data(Data_Mem_Data), .sel(1'b1), .clk(clk), .ld(not_1_out));  // open: clr
  Hex_Digit_Display hex_digit_display_5 (.value(Display_1[15:12]));  // open: dp
  Hex_Digit_Display hex_digit_display_6 (.value(Display_1[11:8]));  // open: dp
  display u_display_1 (
    .sel(disp), .ctrl(bitselector_1_out), .Input_0(Data_1), .Output_0(Display_0), .Output_1(Display_1));
  BitSelector #(.width(16)) bitselector_1 (.in(IMM), .out(bitselector_1_out), .sel(4'b0000));
  Multiplexer #(.width(16), .enable("false")) multiplexer_7 (
    .in0(Data_Mem_Addr), .in1(Data_Mem_Data), .out(multiplexer_7_out), .sel(MemtoReg));
  Hex_Digit_Display hex_digit_display_7 (.value(Display_1[7:4]));  // open: dp
  Hex_Digit_Display hex_digit_display_8 (.value(Display_1[3:0]));  // open: dp
  Multiplexer #(.width(16), .enable("false")) multiplexer_8 (
    .in0(multiplexer_7_out), .in1(dec_inc_pc_3_dec_pc_2), .out(write_data), .sel(jal));
  dec_inc_pc dec_inc_pc_3 (.dec_pc(br_PC), .dec_pc_2(dec_inc_pc_3_dec_pc_2));  // open: inc_pc, inc_pc_2

  // Other names for the same wires on the sheet: ALU_out[15:0] = Data_Mem_Addr; d0[15:0] = Display_0;
  //   d1[15:0] = Display_1; DMD[15:0] = Data_Mem_Data; FIM[15:0] = From_Instr_Mem; MemWrite = Data_Mem_Write;
  //   TIM[15:0] = To_Instr_Mem

  // Notes on the sheet:
  //   kill or not
  //   DECODE
  //   This is a CLK that is an INPUT driven from the harness.
  //   Remember, this circuit is loaded from the harness to be tested!
  //   These are OUTPUTS to the circuit
  //   DO NOT CHANGE THE LOCATIONS OF THE INPUTS/OUTPUTS! IF YOU DO SO, YOU NEED TO MAKE SURE THE PINS ARE AT THE RIGHT PLACE!
  //   pc+1
  //   pc
  //   if jal write to reg 3
  //   regfile
  //   ALU
  //   DISPLAY [0]
  //   These are OUTPUTS to the circuit
  //   DISPLAY [1]
endmodule

module decode_of_cpu (
  input  [15:0] instruction,
  output [1:0] RS,
  output [1:0] RT,
  output [1:0] RD,
  output [5:0] FUNCT,
  output [7:0] IMMEDIATE,
  output [3:0] OPCODE,
  output [11:0] ADDR
);


  assign ADDR = instruction[11:0];
  assign FUNCT = instruction[5:0];
  assign IMMEDIATE = instruction[7:0];
  assign OPCODE = instruction[15:12];
  assign RD = instruction[7:6];
  assign RS = instruction[11:10];
  assign RT = instruction[9:8];

  // Notes on the sheet:
  //   breaks instruction into respective parts
endmodule

module Sign_Extend (
  input  [7:0] imm,
  input  [11:0] addr,
  input  in_3,
  output [15:0] se_addr,
  output [15:0] se_imm
);

  Multiplexer #(.width(16)) multiplexer_1 (
    .in0({4'b0000, addr}), .in1({{5{addr[11]}}, addr[10:0]}), .out(se_addr), .sel(in_3));  // open: en
  Multiplexer #(.width(16)) multiplexer_2 (
    .in0({{8{1'b0}}, imm}), .in1({{9{imm[7]}}, imm[6:0]}), .out(se_imm), .sel(in_3));  // open: en

  // Other names for the same wires on the sheet: s_u = in_3

  // Notes on the sheet:
  //   sign extends address field and immediate field
  //   if unsigned appends zero else sign extends
endmodule

module No_Op (
  input  beq,
  input  equal,
  input  branch,
  input  jr,
  input  jal,
  input  jump,
  output nop
);

  wire and_1_out, and_2_out;

  and and_1 (and_1_out, beq, equal, branch);
  and and_2 (and_2_out, ~equal, ~beq, branch);  // AND_Gate
  or or_1 (nop, and_1_out, and_2_out, jr, jal, jump);
endmodule

module Branch (
  input  [15:0] pc,
  input  [15:0] imm,
  input  branch,
  input  equal,
  input  BEQ_BNE,
  output [15:0] pc_branch
);

  wire and_1_out, and_2_out, or_1_out;
  wire [15:0] adder_1_out, dec_inc_pc_1_dec_pc_2;

  and and_1 (and_1_out, branch, BEQ_BNE, equal);
  and and_2 (and_2_out, ~equal, ~BEQ_BNE, branch);  // AND_Gate
  dec_inc_pc dec_inc_pc_1 (.dec_pc(adder_1_out), .dec_pc_2(dec_inc_pc_1_dec_pc_2));  // open: inc_pc, inc_pc_2
  Adder #(.width(16)) adder_1 (.a(pc), .b(imm), .out(adder_1_out));  // open: cin, cout
  or or_1 (or_1_out, and_1_out, and_2_out);
  Multiplexer #(.width(16), .enable("false")) multiplexer_1 (
    .in0(pc), .in1(dec_inc_pc_1_dec_pc_2), .out(pc_branch), .sel(or_1_out));
endmodule

module ALU_SW (
  input  [3:0] I_type,
  input  [3:0] Rtype,
  input  R_flag,
  output [3:0] alu_switch
);

  Multiplexer #(.width(4), .enable("false")) multiplexer_1 (.in0(I_type), .in1(Rtype), .out(alu_switch), .sel(R_flag));

  // Notes on the sheet:
  //   Determines what type of function alu will execute
endmodule
