// Logisim project Regfile.circ as structural Verilog: 5 circuits, main circuit main
module main (
  input  [1:0] Read_register_1,
  input  [1:0] Read_register_2,
  input  [1:0] write_register,
  input  [15:0] write_data,
  input  RegWrite,
  input  clock,
  output [15:0] Reg_0_Value,
  output [15:0] Reg_1_Value,
  output [15:0] Reg_2_Value,
  output [15:0] Reg_3_Value,
  output [15:0] Read_Data_1,
  output [15:0] Read_Data_2
);

  wire and_1_out, and_2_out, and_3_out, and_4_out, decoder_1_out0, decoder_1_out1, decoder_1_out2,
       decoder_1_out3;
  wire [15:0] demultiplexer_1_out0, demultiplexer_1_out1, demultiplexer_1_out2, demultiplexer_1_out3;

  Decoder #(.select(2), .enable("false")) decoder_1 (
    .out0(decoder_1_out0), .out1(decoder_1_out1), .out2(decoder_1_out2), .out3(decoder_1_out3),
    .sel(write_register));
  and and_1 (and_1_out, decoder_1_out0, RegWrite);
  and and_2 (and_2_out, decoder_1_out1, RegWrite);
  Demultiplexer #(.select(2), .width(16), .enable("false")) demultiplexer_1 (
    .out0(demultiplexer_1_out0), .out1(demultiplexer_1_out1), .out2(demultiplexer_1_out2),
    .out3(demultiplexer_1_out3), .in(write_data), .sel(write_register));
  and and_3 (and_3_out, decoder_1_out2, RegWrite);
  and and_4 (and_4_out, decoder_1_out3, RegWrite);
  Register #(.width(16)) register_1 (
    .D(demultiplexer_1_out0), .en(and_1_out), .Q(Reg_0_Value), .clk(clock));  // open: clr
  Register #(.width(16)) register_2 (
    .D(demultiplexer_1_out1), .en(and_2_out), .Q(Reg_1_Value), .clk(clock));  // open: clr
  Register #(.width(16)) register_3 (
    .D(demultiplexer_1_out2), .en(and_3_out), .Q(Reg_2_Value), .clk(clock));  // open: clr
  Register #(.width(16)) register_4 (
    .D(demultiplexer_1_out3), .en(and_4_out), .Q(Reg_3_Value), .clk(clock));  // open: clr
  Multiplexer #(.select(2), .width(16), .enable("false")) multiplexer_1 (
    .in0(Reg_0_Value), .in1(Reg_1_Value), .in2(Reg_2_Value), .in3(Reg_3_Value), .out(Read_Data_1),
    .sel(Read_register_1));
  Multiplexer #(.select(2), .width(16), .enable("false")) multiplexer_2 (
    .in0(Reg_0_Value), .in1(Reg_1_Value), .in2(Reg_2_Value), .in3(Reg_3_Value), .out(Read_Data_2),
    .sel(Read_register_2));

  // Other names for the same wires on the sheet: CLK = clock; RR1[1:0] = Read_register_1; RR2[1:0] = Read_register_2;
  //   RW = RegWrite; WD[15:0] = write_data; WR[1:0] = write_register

  // Notes on the sheet:
  //   only write when T
endmodule

module Write_ptr_to_Reg (
  input  [15:0] Data,
  input  WriteReg,
  input  [1:0] register_to_point_to,
  input  clk,
  input  Reset,
  output [15:0] Reg_0_Value,
  output [15:0] Reg_1_Value,
  output [15:0] Reg_2_Value,
  output [15:0] Reg_3_Value
);

  wire demultiplexer_1_out0, demultiplexer_1_out1, demultiplexer_1_out2, demultiplexer_1_out3;

  Demultiplexer #(.select(2), .enable("false")) demultiplexer_1 (
    .out0(demultiplexer_1_out0), .out1(demultiplexer_1_out1), .out2(demultiplexer_1_out2),
    .out3(demultiplexer_1_out3), .in(WriteReg), .sel(register_to_point_to));
  Register #(.width(16)) register_1 (.D(Data), .en(demultiplexer_1_out0), .Q(Reg_0_Value), .clk(clk), .clr(Reset));
  Register #(.width(16)) register_2 (.D(Data), .en(demultiplexer_1_out1), .Q(Reg_1_Value), .clk(clk), .clr(Reset));
  Register #(.width(16)) register_3 (.D(Data), .en(demultiplexer_1_out2), .Q(Reg_2_Value), .clk(clk), .clr(Reset));
  Register #(.width(16)) register_4 (.D(Data), .en(demultiplexer_1_out3), .Q(Reg_3_Value), .clk(clk), .clr(Reset));
endmodule

module Read_ptr_to_Reg (
  input  [15:0] Reg_3_Value,
  input  [15:0] Reg_1_Value,
  input  [15:0] Reg_2_Value,
  input  [15:0] Reg_0_Value,
  input  [1:0] register_to_point_to,
  input  clk,
  input  Reset,
  output [15:0] o_p_3,
  output [15:0] out_9,
  output [15:0] out_10,
  output [15:0] out_11
);

  wire demultiplexer_1_out0, demultiplexer_1_out1, demultiplexer_1_out2, demultiplexer_1_out3;

  Demultiplexer #(.select(2), .enable("false")) demultiplexer_1 (
    .out0(demultiplexer_1_out0), .out1(demultiplexer_1_out1), .out2(demultiplexer_1_out2),
    .out3(demultiplexer_1_out3), .in(1'b1), .sel(register_to_point_to));
  Register #(.width(16)) register_1 (.D(Reg_0_Value), .en(demultiplexer_1_out0), .Q(out_11), .clk(clk), .clr(Reset));
  Register #(.width(16)) register_2 (.D(Reg_1_Value), .en(demultiplexer_1_out1), .Q(out_10), .clk(clk), .clr(Reset));
  Register #(.width(16)) register_3 (.D(Reg_2_Value), .en(demultiplexer_1_out2), .Q(out_9), .clk(clk), .clr(Reset));
  Register #(.width(16)) register_4 (.D(Reg_3_Value), .en(demultiplexer_1_out3), .Q(o_p_3), .clk(clk), .clr(Reset));

  // Other names for the same wires on the sheet: o_p_0[15:0] = out_11; o_p_1[15:0] = out_10; o_p_2[15:0] = out_9
endmodule

module _1 (
);

  wire and_1_out, and_2_out, and_3_out, and_4_out, CLK, decoder_1_out0, decoder_1_out1, decoder_1_out2,
       decoder_1_out3, RW;
  wire [1:0] RR1, RR2, WR;
  wire [15:0] demultiplexer_1_out0, demultiplexer_1_out1, demultiplexer_1_out2, demultiplexer_1_out3,
       multiplexer_1_out, multiplexer_2_out, register_1_q, register_2_q, register_3_q, register_4_q, WD;

  Decoder #(.select(2)) decoder_1 (
    .out0(decoder_1_out0), .out1(decoder_1_out1), .out2(decoder_1_out2), .out3(decoder_1_out3), .sel(WR));  // open: en
  and and_1 (and_1_out, decoder_1_out0, RW);
  and and_2 (and_2_out, decoder_1_out1, RW);
  and and_3 (and_3_out, decoder_1_out2, RW);
  and and_4 (and_4_out, decoder_1_out3, RW);
  Demultiplexer #(.select(2), .width(16)) demultiplexer_1 (
    .out0(demultiplexer_1_out0), .out1(demultiplexer_1_out1), .out2(demultiplexer_1_out2),
    .out3(demultiplexer_1_out3), .in(WD), .sel(WR));  // open: en
  Register #(.width(16)) register_1 (
    .D(demultiplexer_1_out0), .en(and_1_out), .Q(register_1_q), .clk(CLK));  // open: clr
  Register #(.width(16)) register_2 (
    .D(demultiplexer_1_out1), .en(and_2_out), .Q(register_2_q), .clk(CLK));  // open: clr
  Register #(.width(16)) register_3 (
    .D(demultiplexer_1_out2), .en(and_3_out), .Q(register_3_q), .clk(CLK));  // open: clr
  Register #(.width(16)) register_4 (
    .D(demultiplexer_1_out3), .en(and_4_out), .Q(register_4_q), .clk(CLK));  // open: clr
  Multiplexer #(.select(2), .width(16)) multiplexer_1 (
    .in0(register_1_q), .in1(register_2_q), .in2(register_3_q), .in3(register_4_q), .out(multiplexer_1_out),
    .sel(RR1));  // open: en
  Multiplexer #(.select(2), .width(16)) multiplexer_2 (
    .in0(register_1_q), .in1(register_2_q), .in2(register_3_q), .in3(register_4_q), .out(multiplexer_2_out),
    .sel(RR2));  // open: en

  // Notes on the sheet:
  //   only write when T
endmodule

module _11 (
  input  [1:0] Read_register_1,
  input  [1:0] Read_register_2,
  input  [1:0] write_register,
  input  [15:0] write_data,
  input  RegWrite,
  input  clock,
  output [15:0] Reg_0_Value,
  output [15:0] Reg_1_Value,
  output [15:0] Reg_2_Value,
  output [15:0] Reg_3_Value,
  output [15:0] Read_Data_1,
  output [15:0] Read_Data_2
);

  wire Reset;
  wire [15:0] read_ptr_to_reg_1_o_p_3, read_ptr_to_reg_1_out_9, read_ptr_to_reg_1_out_10,
       read_ptr_to_reg_1_out_11, read_ptr_to_reg_2_o_p_3, read_ptr_to_reg_2_out_9, read_ptr_to_reg_2_out_10,
       read_ptr_to_reg_2_out_11;

  Write_ptr_to_Reg write_ptr_to_reg_1 (
    .Data(write_data), .register_to_point_to(write_register), .Reg_0_Value(Reg_0_Value),
    .Reg_1_Value(Reg_1_Value), .Reg_2_Value(Reg_2_Value), .Reg_3_Value(Reg_3_Value), .clk(clock),
    .Reset(Reset), .WriteReg(RegWrite));
  Read_ptr_to_Reg read_ptr_to_reg_1 (
    .register_to_point_to(Read_register_1), .o_p_3(read_ptr_to_reg_1_o_p_3), .Reg_0_Value(Reg_0_Value),
    .Reg_1_Value(Reg_1_Value), .Reg_2_Value(Reg_2_Value), .Reg_3_Value(Reg_3_Value), .clk(clock),
    .Reset(Reset), .out_9(read_ptr_to_reg_1_out_9), .out_10(read_ptr_to_reg_1_out_10),
    .out_11(read_ptr_to_reg_1_out_11));
  Multiplexer #(.select(2), .width(16), .enable("false")) multiplexer_1 (
    .in0(read_ptr_to_reg_1_out_11), .in1(read_ptr_to_reg_1_out_10), .in2(read_ptr_to_reg_1_out_9),
    .in3(read_ptr_to_reg_1_o_p_3), .out(Read_Data_1), .sel(Read_register_1));
  Read_ptr_to_Reg read_ptr_to_reg_2 (
    .register_to_point_to(Read_register_2), .o_p_3(read_ptr_to_reg_2_o_p_3), .Reg_0_Value(Reg_0_Value),
    .Reg_1_Value(Reg_1_Value), .Reg_2_Value(Reg_2_Value), .Reg_3_Value(Reg_3_Value), .clk(clock),
    .Reset(Reset), .out_9(read_ptr_to_reg_2_out_9), .out_10(read_ptr_to_reg_2_out_10),
    .out_11(read_ptr_to_reg_2_out_11));
  Multiplexer #(.select(2), .width(16), .enable("false")) multiplexer_2 (
    .in0(read_ptr_to_reg_2_out_11), .in1(read_ptr_to_reg_2_out_10), .in2(read_ptr_to_reg_2_out_9),
    .in3(read_ptr_to_reg_2_o_p_3), .out(Read_Data_2), .sel(Read_register_2));

  // Other names for the same wires on the sheet: clk = clock; Data[15:0] = write_data
endmodule
